// Digital circuit 01_counter.dig as structural Verilog
module _01_counter (
  input  clk,
  input  reset,
  output A,
  output B,
  output C
);

  wire and_1_out, and_2_out, and_3_out, and_4_out, and_5_out, and_6_out, and_7_out, and_8_out, and_9_out,
       and_10_out, and_11_out, and_12_out, and_13_out, not_1_out, not_2_out, not_3_out, not_4_out, or_1_out,
       or_2_out, Z_0_n, Z_1_n;

  not not_1 (not_1_out, reset);
  not not_2 (not_2_out, C);
  not not_3 (not_3_out, Z_1_n);
  not not_4 (not_4_out, Z_0_n);
  and and_1 (and_1_out, Z_0_n, Z_1_n, not_2_out, not_1_out);
  and and_2 (and_2_out, not_4_out, C, not_1_out);
  and and_3 (and_3_out, not_3_out, C, not_1_out);
  and and_4 (and_4_out, Z_0_n, not_3_out, not_1_out);
  and and_5 (and_5_out, not_4_out, Z_1_n, not_1_out);
  and and_6 (and_6_out, not_4_out, not_1_out);
  and and_7 (and_7_out, Z_1_n, not_2_out);
  and and_8 (and_8_out, not_3_out, C);
  and and_9 (and_9_out, Z_0_n, not_3_out);
  and and_10 (and_10_out, not_4_out, Z_1_n);
  or or_1 (or_1_out, and_1_out, and_2_out, and_3_out);
  or or_2 (or_2_out, and_4_out, and_5_out);
  or or_3 (B, and_7_out, and_8_out);
  or or_4 (A, and_9_out, and_10_out);
  and and_11 (and_11_out, not_1_out, or_1_out);
  and and_12 (and_12_out, not_1_out, or_2_out);
  and and_13 (and_13_out, not_1_out, and_6_out);
  D_FF Z_2_n (.D(and_11_out), .C(clk), .Q(C));  // open: nQ
  D_FF u_Z_1_n (.D(and_12_out), .C(clk), .Q(Z_1_n));  // open: nQ
  D_FF u_Z_0_n (.D(and_13_out), .C(clk), .Q(Z_0_n));  // open: nQ
  // Probe state on {C, Z_1_n, Z_0_n}

  // Other names for the same wires on the sheet: Z_2_n = C
endmodule

/* Test case TestCase:
clk reset C B A
0 0 0 0 0 
0 1 0 0 0
1 1 0 0 0
0 0 0 0 0
1 0 0 0 1
0 0 0 0 1
1 0 0 1 1
0 0 0 1 1
1 0 0 1 0
0 0 0 1 0
1 0 1 1 0
0 0 1 1 0
1 0 1 1 1
0 0 1 1 1
1 0 1 0 1
0 0 1 0 1
1 0 1 0 0
0 0 1 0 0
1 0 0 0 0
0 0 0 0 0
1 0 0 0 1
0 0 0 0 1
1 0 0 1 1
0 0 0 1 1
1 0 0 1 0
0 0 0 1 0
1 0 1 1 0
0 0 1 1 0
1 0 1 1 1
0 0 1 1 1
1 0 1 0 1
0 0 1 0 1
1 0 1 0 0
0 0 1 0 0
*/
