// Digital circuit 02_sqrt.dig as structural Verilog
module _02_sqrt (
  input  [15:0] A,
  input  \input ,
  input  clk,
  output busy,
  output [7:0] sqrt
);

  wire and_1_out, and_2_out, and_3_out, comparator_1_eq, comparator_3_gt, comparator_3_lt, comparator_4_eq,
       comparator_5_eq, d_ff_1_nq, finish, input_t, isState0, multiplexer_5_out;
  wire [1:0] d_ff_2_q, multiplexer_1_out, multiplexer_2_out, multiplexer_3_out, multiplexer_4_out;
  wire [7:0] counter_1_out, multiplexer_6_out, sub_1_s;
  wire [15:0] mul_1_mul, mul_2_mul;

  Multiplexer #(.Bits(2)) multiplexer_1 (.sel(input_t), .in_0(2'b00), .in_1(2'b01), .out(multiplexer_1_out));
  Multiplexer #(.Bits(2)) multiplexer_2 (.sel(busy), .in_0(2'b01), .in_1(2'b10), .out(multiplexer_2_out));
  Multiplexer #(.Bits(2)) multiplexer_3 (.sel(finish), .in_0(2'b10), .in_1(2'b11), .out(multiplexer_3_out));
  D_FF d_ff_1 (.D(\input ), .C(clk), .nQ(d_ff_1_nq));  // open: Q
  Multiplexer #(.Selector_Bits(2), .Bits(2)) multiplexer_4 (
    .sel(d_ff_2_q), .in_0(multiplexer_1_out), .in_1(multiplexer_2_out), .in_2(multiplexer_3_out),
    .in_3(2'b00), .out(multiplexer_4_out));
  Multiplexer #(.Selector_Bits(2)) multiplexer_5 (
    .sel(d_ff_2_q), .in_0(1'b0), .in_1(1'b1), .in_2(1'b1), .in_3(1'b0), .out(multiplexer_5_out));
  and and_1 (and_1_out, \input , d_ff_1_nq);
  D_FF #(.Bits(2)) d_ff_2 (.D(multiplexer_4_out), .C(clk), .Q(d_ff_2_q));  // open: nQ
  D_FF d_ff_3 (.D(multiplexer_5_out), .C(clk), .Q(busy));  // open: nQ
  D_FF d_ff_4 (.D(and_1_out), .C(clk), .Q(input_t));  // open: nQ
  Comparator #(.Bits(2)) comparator_1 (.a(d_ff_2_q), .b(2'b10), .eq(comparator_1_eq));  // open: gt, lt
  Comparator #(.Bits(2)) comparator_2 (.a(d_ff_2_q), .b(2'b00), .eq(isState0));  // open: gt, lt
  and and_2 (and_2_out, comparator_3_gt, comparator_1_eq);
  Counter #(.Bits(8)) counter_1 (.en(and_2_out), .C(clk), .clr(1'b0), .out(counter_1_out));  // open: ovf
  Mul #(.Bits(8)) mul_1 (.a(counter_1_out), .b(counter_1_out), .mul(mul_1_mul));
  // Probe on counter_1_out
  // Probe on mul_1_mul
  Sub #(.Bits(8)) sub_1 (.a(counter_1_out), .b(8'h1), .c_i(1'b0), .s(sub_1_s));  // open: c_o
  Comparator #(.Bits(16)) comparator_3 (.a(A), .b(mul_1_mul), .gt(comparator_3_gt), .lt(comparator_3_lt));  // open: eq
  Multiplexer #(.Bits(8)) multiplexer_6 (
    .sel(and_3_out), .in_0(counter_1_out), .in_1(sub_1_s), .out(multiplexer_6_out));
  and and_3 (and_3_out, comparator_1_eq, comparator_3_lt);
  Mul #(.Bits(8)) mul_2 (.a(multiplexer_6_out), .b(multiplexer_6_out), .mul(mul_2_mul));
  Comparator #(.Bits(8)) comparator_4 (.a(multiplexer_6_out), .b(sub_1_s), .eq(comparator_4_eq));  // open: gt, lt
  D_FF #(.Bits(8)) d_ff_5 (.D(multiplexer_6_out), .C(finish), .Q(sqrt));  // open: nQ
  Comparator #(.Bits(16)) comparator_5 (.a(A), .b(mul_2_mul), .eq(comparator_5_eq));  // open: gt, lt
  or or_1 (finish, comparator_5_eq, comparator_4_eq);
endmodule

/* Test case TestCase1:
clk A input sqrt busy
0 0 0 0 0
1 0 0 0 0
0 0 0 0 0
1 0 0 0 0
0 0 1 X X
1 0 1 X X
loop(x,1000)
0 0 0 X X
1 0 0 X X
end loop
0 0 0 0 0
1 0 0 0 0
*/

/* Test case TestCase2:
clk A input sqrt busy
0 0 0 0 0
1 0 0 0 0
0 0 0 0 0
1 0 0 0 0
0 1 1 X X
1 1 1 X X
loop(x,1000)
0 1 0 X X
1 1 0 X X
end loop
0 0 0 1 0
1 0 0 1 0
*/

/* Test case TestCase3:
clk A input sqrt busy
0 0 0 0 0
1 0 0 0 0
0 0 0 0 0
1 0 0 0 0
0 4 1 X X
1 4 1 X X
loop(x,1000)
0 4 0 X X
1 4 0 X X
end loop
0 0 0 2 0
1 0 0 2 0
*/

/* Test case TestCase4:
clk A input sqrt busy
0 0 0 0 0
1 0 0 0 0
0 0 0 0 0
1 0 0 0 0
0 9 1 X X
1 9 1 X X
loop(x,1000)
0 9 0 X X
1 9 0 X X
end loop
0 0 0 3 0
1 0 0 3 0
*/

/* Test case TestCase5:
clk A input sqrt busy
0 0 0 0 0
1 0 0 0 0
0 0 0 0 0
1 0 0 0 0
0 8 1 X X
1 8 1 X X
loop(x,1000)
0 8 0 X X
1 8 0 X X
end loop
0 0 0 2 0
1 0 0 2 0
*/
