// Digital circuit BBBLab10.dig as structural Verilog
module BBBLab10 (
  input  start,
  input  [8:0] N,
  input  reset,
  input  clock,
  output [7:0] displayout,
  output valid,
  output done,
  output [15:0] clockcount
);

  wire and_1_out, and_2_out, and_3_out, and_4_out, and_5_out, and_6_out, and_7_out, and_8_out, and_9_out,
       and_10_out, and_11_out, and_12_out, comparator_1_lt, comparator_2_lt, comparator_3_lt,
       comparator_4_lt, comparator_5_eq, comparator_7_lt, comparator_8_eq, done_t, newR, not_1_out,
       not_2_out, P2, P3;
  wire [7:0] counter_4_out, multiplexer_1_out, ROMFILE_d;
  wire [8:0] A, add_1_s, add_2_s, counter_1_out, counter_6_out, multiplexer_2_out, print, round;

  Comparator #(.Bits(9)) comparator_1 (.a(counter_1_out), .b(N), .eq(P2), .lt(comparator_1_lt));  // open: gt
  and and_1 (and_1_out, start, comparator_1_lt);
  Counter #(.Bits(9)) counter_1 (.en(and_1_out), .C(clock), .clr(reset), .out(counter_1_out));  // open: ovf
  and and_2 (and_2_out, P2, start);
  and and_3 (and_3_out, clock, ~P2, start);  // And
  and and_4 (and_4_out, P2, start);
  and and_5 (and_5_out, P3, start);
  ROM #(.AddrBits(9), .isProgramMemory("true"), .Bits(8)) ROMFILE (.A(counter_1_out), .sel(start), .D(ROMFILE_d));
  Comparator #(.Bits(9)) comparator_2 (.a(A), .b(N), .lt(comparator_2_lt));  // open: gt, eq
  Comparator #(.Bits(8)) comparator_3 (.a(counter_4_out), .b({8{1'b1}}), .lt(comparator_3_lt));  // open: gt, eq
  Comparator #(.Bits(9)) comparator_4 (.a(print), .b(N), .eq(done_t), .lt(comparator_4_lt));  // open: gt
  and and_6 (and_6_out, comparator_2_lt, and_2_out);
  and and_7 (and_7_out, comparator_4_lt, and_5_out);
  Comparator #(.Bits(9)) comparator_5 (.a(round), .b({9{1'b0}}), .eq(comparator_5_eq));  // open: gt, lt
  not not_1 (not_1_out, comparator_5_eq);
  and and_8 (and_8_out, newR, ~done_t, comparator_3_lt, and_4_out);  // And
  Counter #(.Bits(9)) counter_2 (.en(and_7_out), .C(clock), .clr(reset), .out(print));  // open: ovf
  and and_9 (and_9_out, not_1_out, and_6_out);
  Comparator #(.Bits(9)) comparator_6 (.a(A), .b(N), .eq(P3));  // open: gt, lt
  Counter #(.Bits(9)) counter_3 (.en(and_9_out), .C(clock), .clr(reset), .out(A));  // open: ovf
  Counter #(.Bits(8)) counter_4 (.en(and_8_out), .C(clock), .clr(reset), .out(counter_4_out));  // open: ovf
  Multiplexer #(.Bits(8)) multiplexer_1 (.sel(P2), .in_0(ROMFILE_d), .in_1(counter_4_out), .out(multiplexer_1_out));
  Multiplexer #(.Bits(9)) multiplexer_2 (.sel(P3), .in_0(A), .in_1(print), .out(multiplexer_2_out));
  RAMDualPort #(.AddrBits(8), .Bits(9)) ramdualport_1 (
    .A(multiplexer_1_out), .Din(add_1_s), .str(and_3_out), .C(and_3_out), .ld(1'b1), .D(round));
  and and_10 (and_10_out, start, ~done_t);  // And
  Add #(.Bits(9)) add_1 (.a(round), .b({9{1'b0}}), .c_i(1'b1), .s(add_1_s));  // open: c_o
  Comparator #(.Bits(9)) comparator_7 (.a(add_2_s), .b(round), .lt(comparator_7_lt));  // open: gt, eq
  Add #(.Bits(9)) add_2 (.a(counter_6_out), .b(9'h1), .c_i(1'b0), .s(add_2_s));  // open: c_o
  Counter #(.Bits(16)) counter_5 (.en(and_10_out), .C(clock), .clr(1'b0), .out(clockcount));  // open: ovf
  RAMDualPort #(.AddrBits(9), .Bits(8)) RAM (
    .A(multiplexer_2_out), .Din(counter_4_out), .str(and_9_out), .C(clock), .ld(1'b1), .D(displayout));
  Comparator #(.Bits(9)) comparator_8 (.a(round), .b({9{1'b0}}), .eq(comparator_8_eq));  // open: gt, lt
  and and_11 (and_11_out, P2, comparator_7_lt);
  not not_2 (not_2_out, comparator_7_lt);
  or or_1 (newR, not_2_out, comparator_8_eq);
  Counter #(.Bits(9)) counter_6 (.en(and_11_out), .C(clock), .clr(newR), .out(counter_6_out));  // open: ovf
  Seven_Seg_Hex seven_seg_hex_1 (.d(displayout[7:4]), .dp(1'b0));
  and and_12 (and_12_out, P3, start);
  Seven_Seg_Hex seven_seg_hex_2 (.d(displayout[3:0]), .dp(1'b0));
  and and_13 (valid, and_12_out, ~done_t);  // And
  and and_14 (done, P3, done_t);

  // Notes on the sheet:
  //   N: default 511
  //   clock: Hz: 50
  //   contents of ROMFILE (hex, n*v repeats v):
  //   1,5,4,9,6,3,7,8,2
endmodule
