// Digital circuit mark1.dig as structural Verilog
module mark1 (
  input  [8:0] N,
  input  reset,
  input  start,
  input  clock,
  output done,
  output [7:0] displayout,
  output [15:0] clockcount,
  output valid
);

  wire and_2_out, clk_00_Loading, clk_01_Sorting, clk_10_Printing, Clk_Stated, clock_t, comparator_1_eq,
       comparator_1_gt, comparator_2_eq, comparator_2_gt, comparator_6_eq, comparator_7_eq, comparator_8_eq,
       comparator_9_eq, comparator_10_eq, comparator_12_eq, comparator_13_eq, comparator_13_gt,
       comparator_14_gt, comparator_16_eq, comparator_16_lt, comparator_17_eq, comparator_17_gt,
       comparator_18_eq, comparator_18_gt, comparator_19_eq, comparator_19_gt, counter_2_out, counter_4_ovf,
       counter_5_ovf, counterpreset_1_ovf, counterpreset_2_ovf, d_ff_2_nq, d_ff_3_nq, firstRound, full_i__j,
       i_plus__plus, isState00, isState01, isState01_00, isState01_01, isState01_10, isState01_10_0,
       isState01_10_1, or_1_out, or_2_out, or_3_out, or_4_out, or_6_out, or_7_out, or_8_out, or_9_out,
       Str_01_Sorting, Str_Stated, sub_2_s;
  wire [1:0] counter_1_out, counter_3_out, multiplexer_3_out, multiplexer_4_out, multiplexer_7_out,
       multiplexer_12_out, state, State01;
  wire [7:0] Data_A, Data_B, Din_00_Loading, Din_Stated, multiplexer_2_out, multiplexer_6_out, RAM_d;
  wire [8:0] add_1_s, Address_Stated, Ads_00_Loading, Ads_10_Printing, d_ff_4_q, d_ff_5_q, i, i_plus_1,
       i_plus_2, j, j_plus_1, multiplexer_1_out, multiplexer_5_out, multiplexer_14_out, multiplexer_15_out,
       multiplexer_16_out, multiplexer_17_out, N_1, N_2;

  Comparator #(.Bits(9)) comparator_1 (
    .a(Ads_00_Loading), .b(N_1), .gt(comparator_1_gt), .eq(comparator_1_eq));  // open: lt
  Comparator #(.Bits(9)) comparator_2 (
    .a(Ads_10_Printing), .b(N_1), .gt(comparator_2_gt), .eq(comparator_2_eq));  // open: lt
  or or_1 (or_1_out, comparator_1_gt, comparator_1_eq);
  or or_2 (or_2_out, comparator_2_gt, comparator_2_eq);
  Multiplexer #(.Bits(9)) multiplexer_1 (.sel(isState01_10_1), .in_0(i), .in_1(j), .out(multiplexer_1_out));
  Multiplexer #(.Bits(8)) multiplexer_2 (.sel(isState01_10_1), .in_0(Data_A), .in_1(Data_B), .out(multiplexer_2_out));
  Multiplexer #(.Bits(2)) multiplexer_3 (.sel(or_1_out), .in_0(2'b00), .in_1(2'b01), .out(multiplexer_3_out));
  Counter #(.Bits(2)) counter_1 (.en(isState01), .C(clk_01_Sorting), .clr(1'b0), .out(counter_1_out));  // open: ovf
  Multiplexer #(.Bits(2)) multiplexer_4 (.sel(or_2_out), .in_0(2'b10), .in_1(2'b11), .out(multiplexer_4_out));
  Sub #(.Bits(2)) sub_1 (.a(counter_1_out), .b(2'b01), .c_i(1'b0), .s(State01));  // open: c_o
  Counter counter_2 (.en(isState01_10), .C(clk_01_Sorting), .clr(1'b0), .out(counter_2_out));  // open: ovf
  Multiplexer #(.Selector_Bits(2), .Bits(9)) multiplexer_5 (
    .sel(State01), .in_0(i), .in_1(j), .in_2(multiplexer_1_out), .in_3({9{1'b0}}), .out(multiplexer_5_out));
  Multiplexer #(.Selector_Bits(2), .Bits(8)) multiplexer_6 (
    .sel(State01), .in_0(Data_A), .in_1(Data_B), .in_2(multiplexer_2_out), .in_3({8{1'b0}}),
    .out(multiplexer_6_out));
  Multiplexer #(.Bits(2)) multiplexer_7 (.sel(full_i__j), .in_0(2'b01), .in_1(2'b10), .out(multiplexer_7_out));
  // Probe State01- on State01
  Sub sub_2 (.a(counter_2_out), .b(1'b1), .c_i(1'b0), .s(sub_2_s));  // open: c_o
  Multiplexer #(.Selector_Bits(2)) multiplexer_8 (
    .sel(state), .in_0(clk_00_Loading), .in_1(clk_01_Sorting), .in_2(clk_10_Printing), .in_3(1'b0),
    .out(Clk_Stated));
  Multiplexer #(.Selector_Bits(2), .Bits(9)) multiplexer_9 (
    .sel(state), .in_0(Ads_00_Loading), .in_1(multiplexer_5_out), .in_2(Ads_10_Printing), .in_3({9{1'b0}}),
    .out(Address_Stated));
  Multiplexer #(.Selector_Bits(2), .Bits(8)) multiplexer_10 (
    .sel(state), .in_0(Din_00_Loading), .in_1(multiplexer_6_out), .in_2({8{1'b0}}), .in_3({8{1'b0}}),
    .out(Din_Stated));
  Multiplexer #(.Selector_Bits(2)) multiplexer_11 (
    .sel(state), .in_0(1'b1), .in_1(Str_01_Sorting), .in_2(1'b0), .in_3(1'b0), .out(Str_Stated));
  Multiplexer #(.Selector_Bits(2), .Bits(2)) multiplexer_12 (
    .sel(state), .in_0(multiplexer_3_out), .in_1(multiplexer_7_out), .in_2(multiplexer_4_out), .in_3(2'b11),
    .out(multiplexer_12_out));
  Comparator #(.Bits(2)) comparator_3 (.a(state), .b(2'b00), .eq(isState00));  // open: gt, lt
  Comparator #(.Bits(2)) comparator_4 (.a(state), .b(2'b01), .eq(isState01));  // open: gt, lt
  Comparator #(.Bits(2)) comparator_5 (.a(state), .b(2'b10), .eq(done));  // open: gt, lt
  Comparator #(.Bits(2)) comparator_6 (.a(State01), .b(2'b00), .eq(comparator_6_eq));  // open: gt, lt
  Comparator #(.Bits(2)) comparator_7 (.a(State01), .b(2'b01), .eq(comparator_7_eq));  // open: gt, lt
  Comparator #(.Bits(2)) comparator_8 (.a(State01), .b(2'b10), .eq(comparator_8_eq));  // open: gt, lt
  // Probe State01-10- on sub_2_s
  // Probe on Address_Stated
  // Probe on Din_Stated
  Comparator comparator_9 (.a(sub_2_s), .b(1'b0), .eq(comparator_9_eq));  // open: gt, lt
  Comparator comparator_10 (.a(sub_2_s), .b(1'b1), .eq(comparator_10_eq));  // open: gt, lt
  D_FF #(.Bits(2)) d_ff_1 (.D(multiplexer_12_out), .C(clock_t), .Q(state));  // open: nQ
  and and_1 (clk_00_Loading, isState00, clock_t);
  and and_2 (and_2_out, isState01, clock_t);
  and and_3 (clk_10_Printing, done, clock_t);
  and and_4 (isState01_00, isState01, comparator_6_eq);
  and and_5 (isState01_01, isState01, comparator_7_eq);
  and and_6 (isState01_10, isState01, comparator_8_eq);
  and and_7 (isState01_10_0, isState01_10, comparator_9_eq);
  and and_8 (isState01_10_1, isState01_10, comparator_10_eq);
  // Probe on state
  Counter #(.Bits(2)) counter_3 (.en(1'b1), .C(and_2_out), .clr(1'b0), .out(counter_3_out));  // open: ovf
  // Probe on counter_3_out
  Comparator #(.Bits(2)) comparator_11 (.a(counter_3_out), .b(2'b01), .eq(clk_01_Sorting));  // open: gt, lt
  D_FF d_ff_2 (.D(counter_4_ovf), .C(counter_4_ovf), .nQ(d_ff_2_nq));  // open: Q
  D_FF d_ff_3 (.D(counter_5_ovf), .C(counter_5_ovf), .nQ(d_ff_3_nq));  // open: Q
  Counter #(.Bits(9)) counter_4 (
    .en(d_ff_2_nq), .C(clk_00_Loading), .clr(1'b0), .out(Ads_00_Loading), .ovf(counter_4_ovf));
  Counter #(.Bits(9)) counter_5 (
    .en(d_ff_3_nq), .C(clk_10_Printing), .clr(1'b0), .out(Ads_10_Printing), .ovf(counter_5_ovf));
  // Probe on Ads_00_Loading
  and and_9 (clock_t, start, clock);
  ROM #(.AddrBits(9), .isProgramMemory("true"), .Bits(8)) ROMFILE (.A(Ads_00_Loading), .sel(1'b1), .D(Din_00_Loading));
  // Probe on Din_00_Loading
  // Probe on Address_Stated
  RAMDualPort #(.AddrBits(9), .Bits(8)) RAM (
    .A(Address_Stated), .Din(Din_Stated), .str(Str_Stated), .C(Clk_Stated), .ld(1'b1), .D(RAM_d));
  // Probe on i_plus_2
  Multiplexer #(.Bits(8)) multiplexer_13 (.sel(done), .in_0({8{1'b0}}), .in_1(RAM_d), .out(displayout));
  // Probe on RAM_d
  CounterPreset #(.Bits(9)) counterpreset_1 (
    .en(isState01), .C(clock_t), .dir(1'b0), .in(i_plus_2), .ld(or_4_out), .clr(1'b0), .out(j),
    .ovf(counterpreset_1_ovf));
  Multiplexer #(.Bits(9)) multiplexer_14 (.sel(i_plus__plus), .in_0(i), .in_1(i_plus_1), .out(multiplexer_14_out));
  Multiplexer #(.Bits(9)) multiplexer_15 (
    .sel(i_plus__plus), .in_0(j_plus_1), .in_1(i_plus_1), .out(multiplexer_15_out));
  Seven_Seg_Hex seven_seg_hex_1 (.d(displayout[7:4]), .dp(1'b0));
  // Probe on j
  Comparator #(.Bits(9)) comparator_12 (
    .a(multiplexer_14_out), .b(multiplexer_15_out), .eq(comparator_12_eq));  // open: gt, lt
  Add #(.Bits(9)) add_1 (.a(multiplexer_15_out), .b(9'h1), .c_i(1'b0), .s(add_1_s));  // open: c_o
  Seven_Seg_Hex seven_seg_hex_2 (.d(displayout[3:0]), .dp(1'b0));
  Comparator #(.Bits(9)) comparator_13 (.a(j), .b(N_1), .gt(comparator_13_gt), .eq(comparator_13_eq));  // open: lt
  Multiplexer #(.Bits(9)) multiplexer_16 (
    .sel(comparator_12_eq), .in_0(multiplexer_15_out), .in_1(add_1_s), .out(multiplexer_16_out));
  Register #(.Bits(8)) Reg_Ai (.D(RAM_d), .C(clk_01_Sorting), .en(isState01_00), .Q(Data_A));
  Register #(.Bits(8)) Reg_Bj (.D(RAM_d), .C(clk_01_Sorting), .en(isState01_01), .Q(Data_B));
  or or_3 (or_3_out, comparator_13_gt, comparator_13_eq);
  Counter #(.Bits(16)) counter_6 (.en(1'b1), .C(clock_t), .clr(1'b0), .out(clockcount));  // open: ovf
  // Probe on Data_A
  // Probe on Data_B
  Multiplexer #(.Bits(9)) multiplexer_17 (
    .sel(firstRound), .in_0(multiplexer_16_out), .in_1(9'h1), .out(multiplexer_17_out));
  Comparator #(.Bits(8)) comparator_14 (.a(Data_A), .b(Data_B), .gt(comparator_14_gt));  // open: eq, lt
  or or_4 (or_4_out, or_3_out, counterpreset_1_ovf);
  Sub #(.Bits(9)) sub_3 (.a(9'h4), .b(9'h1), .c_i(1'b0), .s(N_1));  // open: c_o
  Add #(.Bits(9)) add_2 (.a(i), .b(9'h1), .c_i(1'b0), .s(i_plus_1));  // open: c_o
  Add #(.Bits(9)) add_3 (.a(j), .b(9'h1), .c_i(1'b0), .s(j_plus_1));  // open: c_o
  Comparator #(.Bits(9)) comparator_15 (.a(j), .b(N_1), .eq(i_plus__plus));  // open: gt, lt
  Comparator #(.Bits(9)) comparator_16 (
    .a(clockcount[8:0]), .b(9'h4), .eq(comparator_16_eq), .lt(comparator_16_lt));  // open: gt
  // Probe swap on comparator_14_gt
  D_FF #(.Bits(9)) d_ff_4 (.D(multiplexer_14_out), .C(clk_01_Sorting), .Q(d_ff_4_q));  // open: nQ
  D_FF #(.Bits(9)) d_ff_5 (.D(multiplexer_17_out), .C(clk_01_Sorting), .Q(d_ff_5_q));  // open: nQ
  Sub #(.Bits(9)) sub_4 (.a(N_1), .b(9'h1), .c_i(1'b0), .s(N_2));  // open: c_o
  Add #(.Bits(9)) add_4 (.a(i_plus_1), .b(9'h1), .c_i(1'b0), .s(i_plus_2));  // open: c_o
  CounterPreset #(.Bits(9)) counterpreset_2 (
    .en(or_4_out), .C(clock_t), .dir(1'b0), .in({9{1'b0}}), .ld(or_9_out), .clr(or_9_out), .out(i),
    .ovf(counterpreset_2_ovf));
  // Probe i on d_ff_4_q
  // Probe j on d_ff_5_q
  or or_5 (firstRound, comparator_16_eq, comparator_16_lt);
  and and_10 (Str_01_Sorting, comparator_14_gt, isState01_10);
  // Probe on i
  Comparator #(.Bits(9)) comparator_17 (.a(i), .b(N_2), .gt(comparator_17_gt), .eq(comparator_17_eq));  // open: lt
  Comparator #(.Bits(9)) comparator_18 (
    .a(d_ff_4_q), .b(N_2), .gt(comparator_18_gt), .eq(comparator_18_eq));  // open: lt
  Comparator #(.Bits(9)) comparator_19 (
    .a(d_ff_5_q), .b(N_1), .gt(comparator_19_gt), .eq(comparator_19_eq));  // open: lt
  or or_6 (or_6_out, comparator_17_gt, comparator_17_eq);
  or or_7 (or_7_out, comparator_18_gt, comparator_18_eq);
  or or_8 (or_8_out, comparator_19_gt, comparator_19_eq);
  and and_11 (full_i__j, or_7_out, or_8_out);
  or or_9 (or_9_out, counterpreset_2_ovf, or_6_out);

  assign valid = done;

  // Other names for the same wires on the sheet: isState10 = done

  // Notes on the sheet:
  //   contents of ROMFILE (hex, n*v repeats v):
  //   4,3,1,2
endmodule
