// Digital circuit mark2.dig as structural Verilog
module mark2 (
  input  [8:0] N,
  input  reset,
  input  start,
  input  clock,
  input  in_9,
  output done,
  output [7:0] displayout,
  output [15:0] clockcount,
  output valid
);

  wire A_gt_B, and_1_out, comparator_1_eq, comparator_9_eq, comparator_9_gt, comparator_10_eq,
       comparator_11_eq, comparator_11_gt, comparator_12_eq, comparator_12_gt, comparator_13_eq,
       comparator_13_gt, comparator_14_eq, comparator_14_gt, counterpreset_1_ovf, counterpreset_2_ovf,
       fullyFirstLoaded, i_plus__plus, isState1_001, isState2_010, isState3_011, isState4_100, isState5_101,
       isState6_110, isState7_111, multiplexer_10_out, not_1_out, notState0_000, or_1_out, or_2_out,
       or_4_out, or_5_out, or_6_out, or_7_out, read_write, sorted;
  wire [2:0] multiplexer_1_out, multiplexer_2_out, multiplexer_3_out, multiplexer_4_out, multiplexer_5_out,
       multiplexer_6_out, multiplexer_7_out, state;
  wire [7:0] D_RAM, D_RegA, D_RegB, Din, multiplexer_9_out, ROMFILE_d;
  wire [8:0] A, A1, A7, add_1_s, d_ff_5_q, d_ff_6_q, i, i_plus_1, i_plus_2, j, j_plus_1, multiplexer_8_out,
       multiplexer_12_out, multiplexer_13_out, multiplexer_14_out, multiplexer_15_out, multiplexer_16_out,
       N_1, N_2;

  Multiplexer #(.Bits(3)) multiplexer_1 (.sel(start), .in_0(3'b000), .in_1(3'b001), .out(multiplexer_1_out));
  Multiplexer #(.Bits(3)) multiplexer_2 (.sel(fullyFirstLoaded), .in_0(3'b001), .in_1(3'b010), .out(multiplexer_2_out));
  Counter #(.Bits(9)) counter_1 (.en(isState1_001), .C(clock), .clr(reset), .out(A1));  // open: ovf
  Counter #(.Bits(9)) counter_2 (.en(isState7_111), .C(clock), .clr(reset), .out(A7));  // open: ovf
  Multiplexer #(.Bits(3)) multiplexer_3 (.sel(sorted), .in_0(3'b010), .in_1(3'b111), .out(multiplexer_3_out));
  ROM #(.AddrBits(9), .isProgramMemory("true"), .Bits(8)) ROMFILE (.A(A1), .sel(isState1_001), .D(ROMFILE_d));
  Multiplexer #(.Bits(3)) multiplexer_4 (
    .sel(A_gt_B), .in_0(multiplexer_3_out), .in_1(3'b101), .out(multiplexer_4_out));
  Multiplexer #(.Bits(3)) multiplexer_5 (.sel(sorted), .in_0(3'b010), .in_1(3'b111), .out(multiplexer_5_out));
  Multiplexer #(.Bits(3), .Selector_Bits(3)) multiplexer_6 (
    .sel(state), .in_0(multiplexer_1_out), .in_1(multiplexer_2_out), .in_2(3'b011), .in_3(3'b100),
    .in_4(multiplexer_4_out), .in_5(3'b110), .in_6(multiplexer_5_out), .in_7(3'b111), .out(multiplexer_6_out));
  Multiplexer #(.Bits(3)) multiplexer_7 (.sel(reset), .in_0(multiplexer_6_out), .in_1(3'b000), .out(multiplexer_7_out));
  Multiplexer #(.Selector_Bits(3), .Bits(9)) multiplexer_8 (
    .sel(state), .in_0({9{1'b0}}), .in_1(A1), .in_2({9{1'b0}}), .in_3(i), .in_4(j), .in_5(i), .in_6(j),
    .in_7(A7), .out(multiplexer_8_out));
  Multiplexer #(.Selector_Bits(3), .Bits(8)) multiplexer_9 (
    .sel(state), .in_0({8{1'b0}}), .in_1(ROMFILE_d), .in_2(D_RAM), .in_3(D_RAM), .in_4(D_RAM), .in_5(D_RegB),
    .in_6(D_RegA), .in_7(D_RAM), .out(multiplexer_9_out));
  Multiplexer #(.Selector_Bits(3)) multiplexer_10 (
    .sel(state), .in_0(1'b1), .in_1(1'b0), .in_2(1'b1), .in_3(1'b1), .in_4(1'b1), .in_5(1'b0), .in_6(1'b0),
    .in_7(1'b1), .out(multiplexer_10_out));
  D_FF #(.Bits(3)) d_ff_1 (.D(multiplexer_7_out), .C(clock), .Q(state));  // open: nQ
  D_FF #(.Bits(9)) d_ff_2 (.D(multiplexer_8_out), .C(clock), .Q(A));  // open: nQ
  D_FF #(.Bits(8)) d_ff_3 (.D(multiplexer_9_out), .C(clock), .Q(Din));  // open: nQ
  D_FF d_ff_4 (.D(multiplexer_10_out), .C(clock), .Q(read_write));  // open: nQ
  // Probe on state
  // Probe on A
  // Probe on Din
  // Probe on i_plus_2
  Seven_Seg_Hex seven_seg_hex_1 (.d(displayout[7:4]), .dp(1'b0));
  CounterPreset #(.Bits(9)) counterpreset_1 (
    .en(isState2_010), .C(clock), .dir(1'b0), .in(i_plus_2), .ld(or_2_out), .clr(1'b0), .out(j),
    .ovf(counterpreset_1_ovf));
  Seven_Seg_Hex seven_seg_hex_2 (.d(displayout[3:0]), .dp(1'b0));
  Multiplexer #(.Bits(8)) multiplexer_11 (.sel(isState7_111), .in_0({8{1'b0}}), .in_1(D_RAM), .out(displayout));
  // Probe on j
  not not_1 (not_1_out, read_write);
  RAMDualPort #(.AddrBits(9), .Bits(8)) RAM (.A(A), .Din(Din), .str(not_1_out), .C(clock), .ld(read_write), .D(D_RAM));
  Comparator #(.Bits(3)) comparator_1 (.a(state), .b(3'b000), .eq(comparator_1_eq));  // open: gt, lt
  Comparator #(.Bits(3)) comparator_2 (.a(state), .b(3'b001), .eq(isState1_001));  // open: gt, lt
  Comparator #(.Bits(3)) comparator_3 (.a(state), .b(3'b010), .eq(isState2_010));  // open: gt, lt
  Comparator #(.Bits(3)) comparator_4 (.a(state), .b(3'b011), .eq(isState3_011));  // open: gt, lt
  Comparator #(.Bits(3)) comparator_5 (.a(state), .b(3'b100), .eq(isState4_100));  // open: gt, lt
  Comparator #(.Bits(3)) comparator_6 (.a(state), .b(3'b101), .eq(isState5_101));  // open: gt, lt
  Comparator #(.Bits(3)) comparator_7 (.a(state), .b(3'b110), .eq(isState6_110));  // open: gt, lt
  Comparator #(.Bits(3)) comparator_8 (.a(state), .b(3'b111), .eq(isState7_111));  // open: gt, lt
  Comparator #(.Bits(9)) comparator_9 (.a(j), .b(N_1), .gt(comparator_9_gt), .eq(comparator_9_eq));  // open: lt
  Counter #(.Bits(16)) counter_3 (.en(notState0_000), .C(clock), .clr(reset), .out(clockcount));  // open: ovf
  // Probe on D_RAM
  not not_2 (notState0_000, comparator_1_eq);
  or or_1 (or_1_out, comparator_9_gt, comparator_9_eq);
  or or_2 (or_2_out, or_1_out, counterpreset_1_ovf);
  Multiplexer #(.Bits(9)) multiplexer_12 (
    .sel(i_plus__plus), .in_0(j_plus_1), .in_1(i_plus_1), .out(multiplexer_12_out));
  Multiplexer #(.Bits(9)) multiplexer_13 (.sel(i_plus__plus), .in_0(i), .in_1(i_plus_1), .out(multiplexer_13_out));
  Multiplexer #(.Bits(9)) multiplexer_14 (
    .sel(fullyFirstLoaded), .in_0({9{1'b0}}), .in_1(multiplexer_12_out), .out(multiplexer_14_out));
  CounterPreset #(.Bits(9)) counterpreset_2 (
    .en(or_2_out), .C(clock), .dir(1'b0), .in({9{1'b0}}), .ld(or_5_out), .clr(or_5_out), .out(i),
    .ovf(counterpreset_2_ovf));
  Comparator #(.Bits(9)) comparator_10 (
    .a(multiplexer_13_out), .b(multiplexer_14_out), .eq(comparator_10_eq));  // open: gt, lt
  // Probe on i
  Comparator #(.Bits(9)) comparator_11 (.a(A), .b(N_1), .gt(comparator_11_gt), .eq(comparator_11_eq));  // open: lt
  Add #(.Bits(9)) add_1 (.a(multiplexer_14_out), .b(9'h1), .c_i(1'b0), .s(add_1_s));  // open: c_o
  Comparator #(.Bits(9)) comparator_12 (.a(i), .b(N_2), .gt(comparator_12_gt), .eq(comparator_12_eq));  // open: lt
  or or_3 (fullyFirstLoaded, comparator_11_gt, comparator_11_eq);
  Multiplexer #(.Bits(9)) multiplexer_15 (
    .sel(comparator_10_eq), .in_0(multiplexer_14_out), .in_1(add_1_s), .out(multiplexer_15_out));
  Multiplexer #(.Bits(9)) multiplexer_16 (
    .sel(fullyFirstLoaded), .in_0({9{1'b0}}), .in_1(multiplexer_15_out), .out(multiplexer_16_out));
  or or_4 (or_4_out, comparator_12_gt, comparator_12_eq);
  // Probe on multiplexer_13_out
  // Probe on multiplexer_16_out
  or or_5 (or_5_out, counterpreset_2_ovf, or_4_out);
  and and_1 (and_1_out, clock, isState2_010);
  D_FF #(.Bits(9)) d_ff_5 (.D(multiplexer_13_out), .C(and_1_out), .Q(d_ff_5_q));  // open: nQ
  D_FF #(.Bits(9)) d_ff_6 (.D(multiplexer_16_out), .C(and_1_out), .Q(d_ff_6_q));  // open: nQ
  // Probe i on d_ff_5_q
  // Probe j on d_ff_6_q
  Register #(.Bits(8)) RegA (.D(D_RAM), .C(clock), .en(isState3_011), .Q(D_RegA));
  Register #(.Bits(8)) RegB (.D(D_RAM), .C(clock), .en(isState4_100), .Q(D_RegB));
  Comparator #(.Bits(9)) comparator_13 (
    .a(d_ff_5_q), .b(N_2), .gt(comparator_13_gt), .eq(comparator_13_eq));  // open: lt
  Comparator #(.Bits(9)) comparator_14 (
    .a(d_ff_6_q), .b(N_1), .gt(comparator_14_gt), .eq(comparator_14_eq));  // open: lt
  // Probe on D_RegA
  // Probe on D_RegB
  or or_6 (or_6_out, comparator_13_gt, comparator_13_eq);
  or or_7 (or_7_out, comparator_14_gt, comparator_14_eq);
  Comparator #(.Bits(8)) comparator_15 (.a(D_RegA), .b(D_RegB), .gt(A_gt_B));  // open: eq, lt
  and and_2 (sorted, or_6_out, or_7_out);
  Sub #(.Bits(9)) sub_1 (.a(N), .b(9'h1), .c_i(1'b0), .s(N_1));  // open: c_o
  Add #(.Bits(9)) add_2 (.a(i), .b(9'h1), .c_i(1'b0), .s(i_plus_1));  // open: c_o
  Add #(.Bits(9)) add_3 (.a(j), .b(9'h1), .c_i(1'b0), .s(j_plus_1));  // open: c_o
  Comparator #(.Bits(9)) comparator_16 (.a(j), .b(N_1), .eq(i_plus__plus));  // open: gt, lt
  Sub #(.Bits(9)) sub_2 (.a(N_1), .b(9'h1), .c_i(1'b0), .s(N_2));  // open: c_o
  Add #(.Bits(9)) add_4 (.a(i_plus_1), .b(9'h1), .c_i(1'b0), .s(i_plus_2));  // open: c_o

  assign done = in_9;
  assign valid = in_9;

  // Notes on the sheet:
  //   contents of ROMFILE (hex, n*v repeats v):
  //   4,3,1,2
endmodule
