// Digital circuit mark4.dig as structural Verilog
module mark4 (
  input  [8:0] N,
  input  reset,
  input  start,
  input  clock,
  output done,
  output [7:0] displayout,
  output [15:0] clockcount,
  output valid
);

  wire isState0, isState1;
  wire [3:0] multiplexer_1_out, multiplexer_2_out, multiplexer_3_out, state;

  Multiplexer #(.Bits(4)) multiplexer_1 (.sel(start), .in_0(4'b0000), .in_1(4'b1111), .out(multiplexer_1_out));
  Multiplexer #(.Bits(4), .Selector_Bits(4)) multiplexer_2 (
    .sel(state), .in_0(multiplexer_1_out), .out(multiplexer_2_out));  // open: in_1, in_2, in_3, in_4, in_5, in_6, in_7, in_8, in_9, in_10, in_11, in_12, in_13, in_14, in_15
  ROM #(.AddrBits(9), .Bits(8)) ROMFILE ();  // open: A, sel, D
  Multiplexer #(.Bits(4)) multiplexer_3 (
    .sel(reset), .in_0(multiplexer_2_out), .in_1(4'b0000), .out(multiplexer_3_out));
  D_FF d_ff_1 (.D(multiplexer_3_out[0]), .C(clock), .Q(state[0]));  // open: nQ
  // Probe on state
  Comparator #(.Bits(4)) comparator_1 (.a(state), .b(4'b0000), .eq(isState0));  // open: gt, lt
  Comparator #(.Bits(4)) comparator_2 (.a(state), .b(4'b0001), .eq(isState1));  // open: gt, lt
  Seven_Seg_Hex seven_seg_hex_1 (.d(displayout[7:4]), .dp(1'b0));
  RAMDualPort #(.AddrBits(9), .Bits(8)) RAM ();  // open: A, Din, str, C, ld, D
  Seven_Seg_Hex seven_seg_hex_2 (.d(displayout[3:0]), .dp(1'b0));
  // Pins of 1 and 4 bits meet at state
  // Pins of 1 and 4 bits meet at multiplexer_3_out
endmodule
