// Digital circuit mark5.dig as structural Verilog
module mark5 (
  input  [8:0] N,
  input  reset,
  input  start,
  input  clock,
  output [7:0] displayout,
  output [15:0] clockcount,
  output valid,
  output done
);

  wire and_1_out, and_2_out, and_3_out, and_4_out, and_5_out, and_6_out, and_7_out, and_8_out, and_9_out,
       and_10_out, and_13_out, comparator_1_lt, comparator_2_lt, comparator_3_lt, comparator_4_lt,
       comparator_5_lt, comparator_6_eq, comparator_7_eq, done_t, isNewR, not_1_out, not_2_out, Path_2,
       Path_3;
  wire [7:0] counter_2_out, multiplexer_2_out, ROMFILE_d;
  wire [8:0] A, add_1_s, add_2_s, counter_1_out, counter_4_out, counter_5_out, D_round, multiplexer_1_out;

  Comparator #(.Bits(9)) comparator_1 (.a(A), .b(N), .eq(Path_3), .lt(comparator_1_lt));  // open: gt
  Comparator #(.Bits(9)) comparator_2 (.a(counter_1_out), .b(N), .eq(Path_2), .lt(comparator_2_lt));  // open: gt
  and and_1 (and_1_out, start, comparator_2_lt);
  and and_2 (and_2_out, Path_2, start);
  and and_3 (and_3_out, Path_2, start);
  and and_4 (and_4_out, Path_3, start);
  Add #(.Bits(9)) add_1 (.a(counter_5_out), .b(9'h1), .c_i(1'b0), .s(add_1_s));  // open: c_o
  and and_5 (and_5_out, comparator_1_lt, and_3_out);
  Comparator #(.Bits(9)) comparator_3 (.a(add_1_s), .b(D_round), .lt(comparator_3_lt));  // open: gt, eq
  Comparator #(.Bits(8)) comparator_4 (.a(counter_2_out), .b({8{1'b1}}), .lt(comparator_4_lt));  // open: gt, eq
  Comparator #(.Bits(9)) comparator_5 (.a(counter_4_out), .b(N), .eq(done_t), .lt(comparator_5_lt));  // open: gt
  not not_1 (not_1_out, comparator_3_lt);
  Comparator #(.Bits(9)) comparator_6 (.a(D_round), .b({9{1'b0}}), .eq(comparator_6_eq));  // open: gt, lt
  not not_2 (not_2_out, comparator_6_eq);
  and and_6 (and_6_out, not_2_out, and_5_out);
  and and_7 (and_7_out, comparator_5_lt, and_4_out);
  and and_8 (and_8_out, Path_2, comparator_3_lt);
  Comparator #(.Bits(9)) comparator_7 (.a({9{1'b0}}), .b(D_round), .eq(comparator_7_eq));  // open: gt, lt
  and and_9 (and_9_out, isNewR, ~done_t, comparator_4_lt, and_2_out);  // And
  or or_1 (isNewR, not_1_out, comparator_7_eq);
  Counter #(.Bits(9)) counter_1 (.en(and_1_out), .C(clock), .clr(reset), .out(counter_1_out));  // open: ovf
  Counter #(.Bits(8)) counter_2 (.en(and_9_out), .C(clock), .clr(reset), .out(counter_2_out));  // open: ovf
  Counter #(.Bits(9)) counter_3 (.en(and_6_out), .C(clock), .clr(reset), .out(A));  // open: ovf
  Counter #(.Bits(9)) counter_4 (.en(and_7_out), .C(clock), .clr(reset), .out(counter_4_out));  // open: ovf
  Counter #(.Bits(9)) counter_5 (.en(and_8_out), .C(clock), .clr(isNewR), .out(counter_5_out));  // open: ovf
  Seven_Seg_Hex seven_seg_hex_1 (.d(displayout[7:4]), .dp(1'b0));
  Seven_Seg_Hex seven_seg_hex_2 (.d(displayout[3:0]), .dp(1'b0));
  and and_10 (and_10_out, start, ~done_t);  // And
  ROM #(.AddrBits(9), .isProgramMemory("true"), .Bits(8)) ROMFILE (.A(counter_1_out), .sel(start), .D(ROMFILE_d));
  Multiplexer #(.Bits(9)) multiplexer_1 (.sel(Path_3), .in_0(A), .in_1(counter_4_out), .out(multiplexer_1_out));
  and and_11 (valid, Path_3, start, ~done_t);  // And
  and and_12 (done, Path_3, done_t);
  Counter #(.Bits(16)) counter_6 (.en(and_10_out), .C(clock), .clr(1'b0), .out(clockcount));  // open: ovf
  RAMDualPort #(.AddrBits(9), .Bits(8)) RAM (
    .A(multiplexer_1_out), .Din(counter_2_out), .str(and_6_out), .C(clock), .ld(1'b1), .D(displayout));
  Multiplexer #(.Bits(8)) multiplexer_2 (.sel(Path_2), .in_0(ROMFILE_d), .in_1(counter_2_out), .out(multiplexer_2_out));
  Add #(.Bits(9)) add_2 (.a(D_round), .b(9'h1), .c_i(1'b0), .s(add_2_s));  // open: c_o
  and and_13 (and_13_out, clock, ~Path_2, start);  // And
  RAMDualPort #(.AddrBits(8), .Bits(9)) ramdualport_1 (
    .A(multiplexer_2_out), .Din(add_2_s), .str(and_13_out), .C(and_13_out), .ld(1'b1), .D(D_round));

  // Other names for the same wires on the sheet: D_display[7:0] = displayout

  // Notes on the sheet:
  //   clock: Hz: 5000
endmodule
