// Digital circuit playground.dig as structural Verilog
module playground (
  input  clock,
  output [2:0] j
);

  wire counterpreset_1_ovf;
  wire [2:0] i, i_plus_1;

  Add #(.Bits(3)) add_1 (.a(i), .b(3'b001), .c_i(1'b0), .s(i_plus_1));  // open: c_o
  CounterPreset #(.Bits(3)) counterpreset_1 (
    .en(1'b1), .C(clock), .dir(1'b0), .in(i_plus_1), .ld(counterpreset_1_ovf), .clr(1'b0), .out(j),
    .ovf(counterpreset_1_ovf));
  CounterPreset #(.Bits(3)) counterpreset_2 (
    .en(counterpreset_1_ovf), .C(clock), .dir(1'b0), .in(3'b000), .ld(1'b0), .clr(1'b0), .out(i));  // open: ovf
  // Probe on i
endmodule
