// Digital circuit Template.dig as structural Verilog
module Template (
  input  A,
  input  B,
  input  C,
  input  D,
  output Z1__gt,
  output Z2__lt,
  output Z3__eq,
  output Z1__gt_2,
  output Z2__lt_2,
  output Z3__eq_2
);

  wire and_1_out, and_2_out, and_3_out, and_4_out, and_5_out, and_6_out, and_7_out, and_8_out, and_9_out,
       and_10_out, and_11_out, and_12_out, and_13_out, not_1_out, not_2_out, not_3_out, not_4_out, or_1_out,
       or_2_out, or_3_out, or_4_out, or_5_out, or_6_out, or_7_out, or_8_out, or_9_out, or_10_out;

  not not_1 (not_1_out, A);
  not not_2 (not_2_out, B);
  not not_3 (not_3_out, C);
  not not_4 (not_4_out, D);
  and and_1 (and_1_out, B, not_3_out, not_4_out);
  and and_2 (and_2_out, A, not_3_out);
  and and_3 (and_3_out, A, B, not_4_out);
  and and_4 (and_4_out, not_1_out, not_2_out, D);
  and and_5 (and_5_out, not_1_out, C);
  and and_6 (and_6_out, not_2_out, C, D);
  and and_7 (and_7_out, not_1_out, not_2_out, not_3_out, not_4_out);
  and and_8 (and_8_out, not_1_out, B, not_3_out, D);
  and and_9 (and_9_out, A, B, C, D);
  and and_10 (and_10_out, A, not_2_out, C, not_4_out);
  or or_1 (or_1_out, not_2_out, C, D);
  or or_2 (or_2_out, not_1_out, C);
  or or_3 (or_3_out, not_1_out, not_2_out, D);
  or or_4 (or_4_out, A, B, not_4_out);
  or or_5 (or_5_out, A, not_3_out);
  or or_6 (or_6_out, B, not_3_out, not_4_out);
  or or_7 (or_7_out, A, B, C, D);
  or or_8 (or_8_out, A, not_2_out, C, not_4_out);
  or or_9 (or_9_out, not_1_out, not_2_out, not_3_out, not_4_out);
  or or_10 (or_10_out, not_1_out, B, not_3_out, D);
  or or_11 (Z1__gt, and_1_out, and_2_out, and_3_out);
  or or_12 (Z2__lt, and_4_out, and_5_out, and_6_out);
  or or_13 (Z3__eq, and_7_out, and_8_out, and_9_out, and_10_out);
  and and_11 (and_11_out, or_1_out, or_2_out, or_3_out);
  and and_12 (and_12_out, or_4_out, or_5_out, or_6_out);
  and and_13 (and_13_out, or_7_out, or_8_out, or_9_out, or_10_out);
  not not_5 (Z1__gt_2, and_11_out);
  not not_6 (Z2__lt_2, and_12_out);
  not not_7 (Z3__eq_2, and_13_out);
endmodule
