// Digital circuit Template.dig as structural Verilog
module Template (
  input  X0,
  input  X1,
  input  Selector,
  input  X2,
  input  X3,
  input  Selector_2,
  output Z,
  output Z_2
);

  wire and_1_out, and_2_out, not_1_out, not_2_out, or_1_out, or_2_out;

  not not_1 (not_1_out, Selector);
  not not_2 (not_2_out, Selector_2);
  and and_1 (and_1_out, X0, not_1_out);
  and and_2 (and_2_out, X1, Selector);
  or or_1 (or_1_out, X2, Selector_2);
  or or_2 (or_2_out, X3, not_2_out);
  or or_3 (Z, and_1_out, and_2_out);
  and and_3 (Z_2, or_1_out, or_2_out);
endmodule
