// Digital circuit Template.dig as structural Verilog
module Template (
  input  [2:0] In,
  input  clk,
  output [7:0] Z
);

  wire and_2_out, and_3_out, and_4_out, and_5_out, and_6_out, and_7_out, and_8_out, and_9_out, not_1_out,
       not_2_out, not_3_out;

  not not_1 (not_1_out, In[2]);
  and and_1 (Z[7], not_1_out, In[2]);
  not not_2 (not_2_out, In[1]);
  not not_3 (not_3_out, In[0]);
  and and_2 (and_2_out, not_1_out, In[1], not_3_out);
  and and_3 (and_3_out, In[2], not_2_out, not_3_out);
  and and_4 (and_4_out, not_1_out, In[1], In[0]);
  and and_5 (and_5_out, In[2], In[1], In[0]);
  and and_6 (and_6_out, not_2_out, not_3_out);
  and and_7 (and_7_out, not_1_out, not_2_out, In[0]);
  and and_8 (and_8_out, In[2], not_2_out);
  and and_9 (and_9_out, In[1], not_3_out);
  or or_1 (Z[6], and_4_out, and_5_out, and_6_out, and_7_out, and_8_out, and_9_out);
  or or_2 (Z[5], and_3_out, and_5_out, and_7_out, and_9_out);
  or or_3 (Z[3], and_4_out, and_7_out, and_8_out);
  or or_4 (Z[2], and_2_out, and_4_out, and_6_out, and_8_out);
  or or_5 (Z[1], and_2_out, and_3_out, and_5_out);
  or or_6 (Z[0], and_3_out, and_7_out, and_9_out);
  Terminal terminal_1 (.D({Z[7:5], Z[7], Z[3:0]}), .C(clk), .en(1'b1));

  assign Z[4] = Z[7];
endmodule
