// Digital circuit Templatet.dig as structural Verilog
module Templatet (
  input  [3:0] In,
  input  [1:0] Selector,
  output [3:0] Output,
  output Y,
  output Y_2,
  output Y_3,
  output Y_4
);

  wire and_1_out, and_2_out, and_3_out, and_4_out, and_5_out, and_6_out, and_7_out, and_8_out, and_9_out,
       and_10_out, and_11_out, and_12_out, and_13_out, and_14_out, and_15_out, and_16_out, and_17_out,
       and_18_out, and_19_out, and_20_out, and_21_out, and_22_out, and_23_out, and_24_out, and_25_out,
       and_26_out, and_27_out, and_28_out, and_29_out, and_30_out, and_31_out, not_1_out, not_2_out,
       not_3_out, not_4_out, not_5_out, not_6_out;

  not not_1 (not_1_out, Selector[1]);
  not not_2 (not_2_out, Selector[0]);
  not not_3 (not_3_out, In[3]);
  not not_4 (not_4_out, In[2]);
  not not_5 (not_5_out, In[1]);
  not not_6 (not_6_out, In[0]);
  and and_1 (and_1_out, Selector[1], Selector[0], not_3_out, In[1], In[0]);
  and and_2 (and_2_out, Selector[1], not_3_out, In[2], not_5_out, In[0]);
  and and_3 (and_3_out, not_2_out, not_3_out, In[2], In[1]);
  and and_4 (and_4_out, not_2_out, not_3_out, In[2], In[0]);
  and and_5 (and_5_out, In[3], not_4_out, not_5_out);
  and and_6 (and_6_out, not_1_out, Selector[0], In[3], not_4_out, not_5_out);
  and and_7 (and_7_out, Selector[1], not_2_out, In[3], not_4_out, not_5_out);
  and and_8 (and_8_out, not_1_out, not_2_out, not_4_out, not_5_out, In[0]);
  and and_9 (and_9_out, Selector[1], Selector[0], not_4_out, not_5_out, In[0]);
  and and_10 (and_10_out, Selector[1], not_3_out, In[2], In[1]);
  and and_11 (and_11_out, not_1_out, not_2_out, not_3_out, not_4_out, In[1]);
  and and_12 (and_12_out, not_1_out, Selector[0], not_3_out, In[2], not_5_out, In[0]);
  and and_13 (and_13_out, not_1_out, not_3_out, In[2], not_5_out, not_6_out);
  and and_14 (and_14_out, Selector[1], not_3_out, In[2], not_6_out);
  and and_15 (and_15_out, Selector[0], not_3_out, In[2], In[1]);
  and and_16 (and_16_out, Selector[1], Selector[0], not_3_out, In[1], not_6_out);
  and and_17 (and_17_out, not_1_out, not_2_out, not_3_out, In[1], In[0]);
  and and_18 (and_18_out, not_1_out, Selector[0], not_3_out, not_4_out, In[1]);
  and and_19 (and_19_out, not_1_out, not_2_out, not_4_out, not_5_out, not_6_out);
  and and_20 (and_20_out, Selector[1], not_2_out, not_3_out, not_4_out, In[1]);
  and and_21 (and_21_out, not_1_out, Selector[0], not_3_out, In[2], not_5_out, In[0]);
  and and_22 (and_22_out, not_1_out, not_3_out, In[2], not_5_out, not_6_out);
  and and_23 (and_23_out, Selector[1], not_3_out, In[2], not_5_out, In[0]);
  and and_24 (and_24_out, Selector[1], In[3], not_4_out, not_5_out);
  and and_25 (and_25_out, not_1_out, not_2_out, not_3_out, not_6_out);
  and and_26 (and_26_out, Selector[1], not_4_out, not_5_out, In[0]);
  and and_27 (and_27_out, not_1_out, not_2_out, not_4_out, not_5_out, not_6_out);
  and and_28 (and_28_out, not_1_out, Selector[0], not_3_out, In[2], not_5_out, In[0]);
  and and_29 (and_29_out, not_1_out, not_3_out, In[1], not_6_out);
  and and_30 (and_30_out, Selector[1], not_3_out, In[0]);
  and and_31 (and_31_out, Selector[0], not_4_out, not_5_out, In[0]);
  or or_1 (Output[3], and_1_out, and_2_out, and_3_out, and_4_out, and_5_out);
  or or_2 (Output[0], and_25_out, and_26_out, and_27_out, and_28_out, and_29_out, and_30_out, and_31_out);
  or or_3 (Output[2], and_6_out, and_7_out, and_8_out, and_9_out, and_10_out, and_11_out, and_12_out, and_13_out, and_14_out, and_15_out);
  or or_4 (Output[1], and_16_out, and_17_out, and_18_out, and_19_out, and_20_out, and_21_out, and_22_out, and_23_out, and_24_out);

  assign Y = Output[3];
  assign Y_2 = Output[2];
  assign Y_3 = Output[1];
  assign Y_4 = Output[0];
endmodule
