// Digital circuit Template.dig as structural Verilog
module Template (
  input  [6:0] In,
  output [6:0] Output
);

  wire and_2_out, and_3_out, and_4_out, and_5_out, and_6_out, and_7_out, and_8_out, not_8_out, not_9_out,
       not_10_out, xor_8_out, xor_9_out, xor_10_out;

  // Not not_1 has open pins: in=In[6], out=open
  // Not not_2 has open pins: in=In[5], out=open
  xor xor_1 (Output[0], and_2_out, In[6]);
  // Not not_3 has open pins: in=In[4], out=open
  xor xor_2 (Output[1], and_3_out, In[5]);
  xor xor_3 (Output[2], and_4_out, In[4]);
  // Not not_4 has open pins: in=In[3], out=open
  xor xor_4 (Output[3], and_5_out, In[3]);
  // Not not_5 has open pins: in=In[2], out=open
  // Not not_6 has open pins: in=In[1], out=open
  xor xor_5 (Output[4], and_6_out, In[2]);
  // Not not_7 has open pins: in=In[0], out=open
  xor xor_6 (Output[5], and_7_out, In[1]);
  xor xor_7 (Output[6], and_8_out, In[0]);
  xor xor_8 (xor_8_out, In[3], In[2], In[1], In[0]);
  xor xor_9 (xor_9_out, In[5], In[4], In[1], In[0]);
  xor xor_10 (xor_10_out, In[6], In[4], In[2], In[0]);
  not not_8 (not_8_out, xor_8_out);
  not not_9 (not_9_out, xor_9_out);
  not not_10 (not_10_out, xor_10_out);
  // And and_1 has open pins: In_1=not_8_out, In_2=not_9_out, In_3=not_10_out, out=open
  and and_2 (and_2_out, not_8_out, not_9_out, xor_10_out);
  and and_3 (and_3_out, not_8_out, xor_9_out, not_10_out);
  and and_4 (and_4_out, not_8_out, xor_9_out, xor_10_out);
  and and_5 (and_5_out, xor_8_out, not_9_out, not_10_out);
  and and_6 (and_6_out, xor_8_out, not_9_out, xor_10_out);
  and and_7 (and_7_out, xor_8_out, xor_9_out, not_10_out);
  and and_8 (and_8_out, xor_8_out, xor_9_out, xor_10_out);
endmodule
