// Digital circuit Template.dig as structural Verilog
module Template (
  input  [7:0] In,
  output [8:0] Output
);

  wire add_1_c_o;
  wire [7:0] not_1_out;

  assign not_1_out = ~In;  // Not not_1, 8 bits wide
  Add #(.Bits(8)) add_1 (.a(not_1_out), .b(8'h1), .c_i(1'b0), .s(Output[7:0]), .c_o(add_1_c_o));
  not not_2 (Output[8], add_1_c_o);
endmodule
