// Digital circuit Template.dig as structural Verilog
module Template (
  input  [3:0] In,
  input  [3:0] In_2,
  output [3:0] Output,
  output [2:0] Output_2,
  output [3:0] Output_3
);

  wire add_2_c_o, add_3_c_o;
  wire [2:0] add_1_s, multiplexer_1_out, multiplexer_3_out, not_1_out, not_2_out;

  assign not_1_out = ~In[2:0];  // Not not_1, 3 bits wide
  assign not_2_out = ~In_2[2:0];  // Not not_2, 3 bits wide
  Add #(.Bits(3)) add_1 (.a(not_1_out), .b(3'b000), .c_i(1'b1), .s(add_1_s));  // open: c_o
  Multiplexer #(.Bits(3)) multiplexer_1 (.sel(In[3]), .in_0(In[2:0]), .in_1(add_1_s), .out(multiplexer_1_out));
  Add add_2 (.a(not_2_out[0]), .b(1'b1), .c_i(1'b0), .s(Output_2[0]), .c_o(add_2_c_o));
  Multiplexer #(.Selector_Bits(3), .Bits(4)) multiplexer_2 (
    .sel(In[2:0]), .in_0(4'b0000), .in_1({In[3], multiplexer_1_out}), .in_2({In[3], multiplexer_1_out}),
    .in_3({In[3], multiplexer_1_out}), .in_4({In[3], multiplexer_1_out}), .in_5({In[3], multiplexer_1_out}),
    .in_6({In[3], multiplexer_1_out}), .in_7({In[3], multiplexer_1_out}), .out(Output_3));
  Add add_3 (.a(not_2_out[1]), .b(1'b0), .c_i(add_2_c_o), .s(Output_2[1]), .c_o(add_3_c_o));
  Add add_4 (.a(not_2_out[2]), .b(1'b0), .c_i(add_3_c_o), .s(Output_2[2]));  // open: c_o
  Multiplexer #(.Bits(3)) multiplexer_3 (.sel(In_2[3]), .in_0(In_2[2:0]), .in_1(Output_2), .out(multiplexer_3_out));
  Multiplexer #(.Bits(4), .Selector_Bits(3)) multiplexer_4 (
    .sel(In_2[2:0]), .in_0(4'b0000), .in_1({In_2[3], multiplexer_3_out}),
    .in_2({In_2[3], multiplexer_3_out}), .in_3({In_2[3], multiplexer_3_out}),
    .in_4({In_2[3], multiplexer_3_out}), .in_5({In_2[3], multiplexer_3_out}),
    .in_6({In_2[3], multiplexer_3_out}), .in_7({In_2[3], multiplexer_3_out}), .out(Output));
endmodule
