// Digital circuit Template.dig as structural Verilog
module Template (
  input  [3:0] A,
  input  [3:0] B,
  input  [2:0] S,
  input  M,
  input  C,
  output [3:0] F
);

  wire [2:0] not_1_out, not_3_out;
  wire [3:0] A_t, add_3_s, add_4_s, add_5_s, add_6_s, add_7_s, add_8_s, add_9_s, and_1_out, and_2_out, B_t,
       nand_1_out, nor_1_out, not_5_out, not_6_out, or_1_out, xnor_1_out;

  assign not_1_out = ~A[2:0];  // Not not_1, 3 bits wide
  Add #(.Bits(3)) add_1 (.a(not_1_out), .b(3'b001), .c_i(1'b0), .s(A_t[2:0]));  // open: c_o
  not not_2 (A_t[3], A[3]);
  assign not_3_out = ~B[2:0];  // Not not_3, 3 bits wide
  Add #(.Bits(3)) add_2 (.a(not_3_out), .b(3'b001), .c_i(1'b0), .s(B_t[2:0]));  // open: c_o
  not not_4 (B_t[3], B[3]);
  assign not_5_out = ~A;  // Not not_5, 4 bits wide
  assign not_6_out = ~B;  // Not not_6, 4 bits wide
  assign nand_1_out = ~(A & B);  // NAnd nand_1, 4 bits wide
  assign nor_1_out = ~(A | B);  // NOr nor_1, 4 bits wide
  assign xnor_1_out = ~(A ^ B);  // XNOr xnor_1, 4 bits wide
  assign and_1_out = A & B;  // And and_1, 4 bits wide
  assign or_1_out = A | B;  // Or or_1, 4 bits wide
  assign and_2_out = A & not_6_out;  // And and_2, 4 bits wide
  Add #(.Bits(4)) add_3 (.a(A), .b(4'b0000), .c_i(C), .s(add_3_s));  // open: c_o
  Add #(.Bits(4)) add_4 (.a(A), .b(4'b1111), .c_i(C), .s(add_4_s));  // open: c_o
  Add #(.Bits(4)) add_5 (.a(A), .b(B), .c_i(C), .s(add_5_s));  // open: c_o
  Add #(.Bits(4)) add_6 (.a(A), .b(B_t), .c_i(C), .s(add_6_s));  // open: c_o
  Add #(.Bits(4)) add_7 (.a(A_t), .b(4'b1111), .c_i(C), .s(add_7_s));  // open: c_o
  Add #(.Bits(4)) add_8 (.a(4'b0000), .b(B), .c_i(C), .s(add_8_s));  // open: c_o
  Add #(.Bits(4)) add_9 (.a(add_6_s), .b(4'b1111), .c_i(1'b0), .s(add_9_s));  // open: c_o
  Multiplexer #(.Bits(4), .Selector_Bits(4)) multiplexer_1 (
    .sel({M, S}), .in_0(not_5_out), .in_1(nand_1_out), .in_2(nor_1_out), .in_3(xnor_1_out), .in_4(and_1_out),
    .in_5(or_1_out), .in_6(and_2_out), .in_7(A), .in_8(add_3_s), .in_9(add_4_s), .in_10(add_5_s),
    .in_11(add_9_s), .in_12(add_7_s), .in_13(add_8_s), .in_14({A[2:0], 1'b0}), .in_15({1'b0, A[3:1]}), .out(F));
endmodule
