// Digital circuit Counter74163.dig as structural Verilog
module Counter74163 (
  input  P,
  input  T,
  input  D,
  input  C,
  input  B,
  input  A,
  input  Clr,
  input  Load,
  input  Clock,
  output QD,
  output QC,
  output QB,
  output QA,
  output RCO
);

  wire and_1_out, and_2_out, and_3_out, and_4_out, and_5_out, and_6_out, and_7_out, and_8_out, and_9_out,
       and_10_out, multiplexer_1_out, multiplexer_2_out, multiplexer_3_out, multiplexer_4_out,
       multiplexer_5_out, multiplexer_6_out, multiplexer_7_out, multiplexer_8_out, multiplexer_9_out,
       multiplexer_10_out, multiplexer_11_out, multiplexer_12_out, not_1_out, not_2_out, not_3_out,
       not_4_out, or_1_out, or_2_out, or_3_out;

  not not_1 (not_1_out, QD);
  not not_2 (not_2_out, QC);
  not not_3 (not_3_out, QB);
  not not_4 (not_4_out, QA);
  and and_1 (and_1_out, QA, QB, QC, not_1_out);
  and and_2 (and_2_out, not_4_out, QD);
  and and_3 (and_3_out, not_3_out, QD);
  and and_4 (and_4_out, not_2_out, QD);
  and and_5 (and_5_out, QA, QB, not_2_out);
  and and_6 (and_6_out, not_4_out, QC);
  and and_7 (and_7_out, not_3_out, QC);
  and and_8 (and_8_out, QA, not_3_out);
  and and_9 (and_9_out, not_4_out, QB);
  or or_1 (or_1_out, and_1_out, and_2_out, and_3_out, and_4_out);
  or or_2 (or_2_out, and_5_out, and_6_out, and_7_out);
  or or_3 (or_3_out, and_8_out, and_9_out);
  Multiplexer multiplexer_1 (.sel(Clr), .in_0(1'b0), .in_1(or_1_out), .out(multiplexer_1_out));
  Multiplexer multiplexer_2 (.sel(Clr), .in_0(1'b0), .in_1(or_2_out), .out(multiplexer_2_out));
  Multiplexer multiplexer_3 (.sel(Clr), .in_0(1'b0), .in_1(or_3_out), .out(multiplexer_3_out));
  Multiplexer multiplexer_4 (.sel(Clr), .in_0(1'b0), .in_1(not_4_out), .out(multiplexer_4_out));
  and and_10 (and_10_out, P, T);
  Multiplexer multiplexer_5 (.sel(and_10_out), .in_0(QD), .in_1(multiplexer_1_out), .out(multiplexer_5_out));
  Multiplexer multiplexer_6 (.sel(and_10_out), .in_0(QC), .in_1(multiplexer_2_out), .out(multiplexer_6_out));
  Multiplexer multiplexer_7 (.sel(and_10_out), .in_0(QB), .in_1(multiplexer_3_out), .out(multiplexer_7_out));
  Multiplexer multiplexer_8 (.sel(and_10_out), .in_0(QA), .in_1(multiplexer_4_out), .out(multiplexer_8_out));
  Multiplexer multiplexer_9 (.sel(Load), .in_0(D), .in_1(multiplexer_5_out), .out(multiplexer_9_out));
  Multiplexer multiplexer_10 (.sel(Load), .in_0(C), .in_1(multiplexer_6_out), .out(multiplexer_10_out));
  Multiplexer multiplexer_11 (.sel(Load), .in_0(B), .in_1(multiplexer_7_out), .out(multiplexer_11_out));
  Multiplexer multiplexer_12 (.sel(Load), .in_0(A), .in_1(multiplexer_8_out), .out(multiplexer_12_out));
  D_FF Q_3_n (.D(multiplexer_9_out), .C(Clock), .Q(QD));  // open: nQ
  D_FF Q_2_n (.D(multiplexer_10_out), .C(Clock), .Q(QC));  // open: nQ
  D_FF Q_1_n (.D(multiplexer_11_out), .C(Clock), .Q(QB));  // open: nQ
  D_FF Q_0_n (.D(multiplexer_12_out), .C(Clock), .Q(QA));  // open: nQ
  and and_11 (RCO, QD, QC, QB, QA);

  // Other names for the same wires on the sheet: Q_0_n = QA; Q_1_n = QB; Q_2_n = QC; Q_3_n = QD
endmodule
