// Digital circuit HoF488472.dig as structural Verilog
module HoF488472 (
  input  P,
  input  T,
  input  A,
  input  B,
  input  C,
  input  D,
  input  Clr,
  input  Load,
  input  Clock,
  output RCO,
  output QA,
  output QB,
  output QC,
  output QD
);

  wire add_1_c_o, Count;
  wire [3:0] add_1_s, multiplexer_1_out, multiplexer_2_out, multiplexer_3_out;

  and and_1 (Count, T, P);
  Add #(.Bits(4)) add_1 (.a({QD, QC, QB, QA}), .b(4'b0001), .c_i(1'b0), .s(add_1_s), .c_o(add_1_c_o));
  Multiplexer #(.Bits(4)) multiplexer_1 (.sel(Count), .in_0({QD, QC, QB, QA}), .in_1(add_1_s), .out(multiplexer_1_out));
  and and_2 (RCO, add_1_c_o, T);
  Multiplexer #(.Bits(4)) multiplexer_2 (
    .sel(Load), .in_0({D, C, B, A}), .in_1(multiplexer_3_out), .out(multiplexer_2_out));
  Multiplexer #(.Bits(4)) multiplexer_3 (.sel(Clr), .in_0(4'b0000), .in_1(multiplexer_1_out), .out(multiplexer_3_out));
  D_FF #(.Bits(4)) d_ff_1 (.D(multiplexer_2_out), .C(Clock), .Q({QD, QC, QB, QA}));  // open: nQ
  // Probe on {QD, QC, QB, QA}

  // Other names for the same wires on the sheet: Q[3:0] = {QD, QC, QB, QA}
endmodule
