// Digital circuit Send_Mealy.dig as structural Verilog
module Send_Mealy (
  input  P,
  input  Clr,
  input  clock,
  output Z
);

  wire and_1_out, d_ff_as_1_nq;

  D_FF_AS d_ff_as_1 (.Set(1'b0), .D(P), .C(clock), .Clr(Clr), .nQ(d_ff_as_1_nq));  // open: Q
  and and_1 (and_1_out, P, d_ff_as_1_nq);
  D_FF_AS d_ff_as_2 (.Set(1'b0), .D(and_1_out), .C(clock), .Clr(Clr), .Q(Z));  // open: nQ
endmodule
