// Digital circuit Send_MooreDAS.dig as structural Verilog
module Send_MooreDAS (
  input  P,
  input  Clr,
  input  clock,
  output Z
);

  wire d_ff_as_1_q, d_ff_as_2_nq;

  D_FF_AS d_ff_as_1 (.Set(1'b0), .D(P), .C(clock), .Clr(Clr), .Q(d_ff_as_1_q));  // open: nQ
  D_FF_AS d_ff_as_2 (.Set(1'b0), .D(d_ff_as_1_q), .C(clock), .Clr(Clr), .nQ(d_ff_as_2_nq));  // open: Q
  and and_1 (Z, d_ff_as_1_q, d_ff_as_2_nq);
endmodule
