// Digital circuit HoF501254_ShortestCode .dig as structural Verilog
module HoF501254_ShortestCode (
  input  P5,
  input  reset,
  input  clock,
  input  P10,
  input  P20,
  input  Pcoffee,
  input  Ptea,
  input  Pchange,
  input  Pnext,
  output [5:0] Balance,
  output CoffeeOut,
  output TeaOut,
  output [1:0] Change5,
  output [1:0] Change10,
  output [1:0] Change20
);

  wire and_1_out, and_2_out, and_3_out, and_4_out, ccoff, comparator_1_gt, comparator_2_eq, comparator_2_gt,
       comparator_3_eq, comparator_3_gt, ctea, nor_1_out, ocoff, ocoff_t, or_1_out, or_2_out, or_3_out,
       or_4_out, or_5_out, otea, otea_t, s, s_t;
  wire [1:0] ch5, ch5_t, ch10, ch10_t, ch20, ch20_t, div_1_q, div_2_q, div_2_r, lookuptable_1_out;
  wire [5:0] add_1_s, b, b_t, badd, bsup, div_1_r, lookuptable_2_out, multiplexer_6_out, multiplexer_7_out,
       multiplexer_9_out, sub_1_s, sub_2_s;
  wire [5:2] div_1_q_2, div_2_q_2, div_2_r_2;

  or or_1 (or_1_out, Pcoffee, Ptea);
  and and_1 (and_1_out, or_1_out, ~s_t);  // And
  LookUpTable #(.Bits(2)) lookuptable_1 (.in0(and_4_out), .in1(and_1_out), .in2(Pchange), .out(lookuptable_1_out));
  Multiplexer multiplexer_1 (.sel(s), .in_0(1'b0), .in_1(or_3_out), .out(ocoff));
  and and_2 (and_2_out, Ptea, ctea);
  and and_3 (and_3_out, Pcoffee, ccoff);
  and and_4 (and_4_out, or_5_out, ~s_t);  // And
  Multiplexer #(.Selector_Bits(2), .Bits(6)) multiplexer_2 (
    .sel(lookuptable_1_out), .in_0(b_t), .in_1(badd), .in_2(bsup), .in_3({6{1'b0}}), .out(b));
  or or_2 (or_2_out, and_3_out, and_2_out);
  or or_3 (or_3_out, and_3_out, ocoff_t);
  or or_4 (or_4_out, and_2_out, otea_t);
  Multiplexer multiplexer_3 (.sel(s), .in_0(1'b0), .in_1(or_4_out), .out(otea));
  LookUpTable #(.Bits(6)) lookuptable_2 (.in0(P5), .in1(P10), .in2(P20), .out(lookuptable_2_out));
  or or_5 (or_5_out, P20, P10, P5);
  Multiplexer multiplexer_4 (.sel(s_t), .in_0(or_2_out), .in_1(nor_1_out), .out(s));
  nor nor_1 (nor_1_out, Pchange, Pnext);
  D_FF_AS d_ff_as_1 (.Set(1'b0), .D(s), .C(clock), .Clr(reset), .Q(s_t));  // open: nQ
  Add #(.Bits(6)) add_1 (.a(b_t), .b(lookuptable_2_out), .c_i(1'b0), .s(add_1_s));  // open: c_o
  Multiplexer #(.Bits(6)) multiplexer_5 (.sel(comparator_1_gt), .in_0(add_1_s), .in_1(b_t), .out(badd));
  Comparator #(.Bits(6)) comparator_1 (.a(add_1_s), .b(6'b110010), .gt(comparator_1_gt));  // open: eq, lt
  Sub #(.Bits(6)) sub_1 (.a(b_t), .b(6'b011001), .c_i(1'b0), .s(sub_1_s));  // open: c_o
  Comparator #(.Bits(6)) comparator_2 (.a(b_t), .b(6'b011001), .gt(comparator_2_gt), .eq(comparator_2_eq));  // open: lt
  Multiplexer #(.Bits(6)) multiplexer_6 (.sel(Pcoffee), .in_0(b_t), .in_1(multiplexer_7_out), .out(multiplexer_6_out));
  Multiplexer #(.Bits(6)) multiplexer_7 (.sel(ccoff), .in_0(b_t), .in_1(sub_1_s), .out(multiplexer_7_out));
  or or_6 (ccoff, comparator_2_gt, comparator_2_eq);
  D_FF_AS #(.Bits(6)) d_ff_as_2 (.Set(1'b0), .D(b), .C(clock), .Clr(reset), .Q(b_t));  // open: nQ
  D_FF_AS d_ff_as_3 (.Set(1'b0), .D(ocoff), .C(clock), .Clr(reset), .Q(ocoff_t));  // open: nQ
  D_FF d_ff_1 (.D(ocoff_t), .C(clock), .Q(CoffeeOut));  // open: nQ
  Multiplexer #(.Bits(6)) multiplexer_8 (.sel(Ptea), .in_0(multiplexer_6_out), .in_1(multiplexer_9_out), .out(bsup));
  Multiplexer #(.Bits(6)) multiplexer_9 (.sel(ctea), .in_0(b_t), .in_1(sub_2_s), .out(multiplexer_9_out));
  Sub #(.Bits(6)) sub_2 (.a(b_t), .b(6'b010100), .c_i(1'b0), .s(sub_2_s));  // open: c_o
  Div #(.Bits(6)) div_1 (.a(Balance), .b(6'b010100), .q({div_1_q_2, div_1_q}), .r(div_1_r));
  Div #(.Bits(6)) div_2 (.a(div_1_r), .b(6'b001010), .q({div_2_q_2, div_2_q}), .r({div_2_r_2, div_2_r}));
  D_FF #(.Bits(6)) d_ff_2 (.D(b_t), .C(clock), .Q(Balance));  // open: nQ
  D_FF_AS d_ff_as_4 (.Set(1'b0), .D(otea), .C(clock), .Clr(reset), .Q(otea_t));  // open: nQ
  or or_7 (ctea, comparator_3_gt, comparator_3_eq);
  Comparator #(.Bits(6)) comparator_3 (.a(b_t), .b(6'b010100), .gt(comparator_3_gt), .eq(comparator_3_eq));  // open: lt
  Multiplexer #(.Bits(2)) multiplexer_10 (.sel(Pchange), .in_0(ch20_t), .in_1(div_1_q), .out(ch20));
  Multiplexer #(.Bits(2)) multiplexer_11 (.sel(Pchange), .in_0(ch10_t), .in_1(div_2_q), .out(ch10));
  Multiplexer #(.Bits(2)) multiplexer_12 (.sel(Pchange), .in_0(ch5_t), .in_1(div_2_r), .out(ch5));
  D_FF d_ff_3 (.D(otea_t), .C(clock), .Q(TeaOut));  // open: nQ
  D_FF_AS #(.Bits(2)) d_ff_as_5 (.Set(1'b0), .D(ch5), .C(clock), .Clr(reset), .Q(ch5_t));  // open: nQ
  D_FF #(.Bits(2)) d_ff_4 (.D(ch5_t), .C(clock), .Q(Change5));  // open: nQ
  D_FF_AS #(.Bits(2)) d_ff_as_6 (.Set(1'b0), .D(ch10), .C(clock), .Clr(reset), .Q(ch10_t));  // open: nQ
  D_FF #(.Bits(2)) d_ff_5 (.D(ch10_t), .C(clock), .Q(Change10));  // open: nQ
  D_FF_AS #(.Bits(2)) d_ff_as_7 (.Set(1'b0), .D(ch20), .C(clock), .Clr(reset), .Q(ch20_t));  // open: nQ
  D_FF #(.Bits(2)) d_ff_6 (.D(ch20_t), .C(clock), .Q(Change20));  // open: nQ

  // Other names for the same wires on the sheet: clk = clock; pch = Pchange; pcoff = Pcoffee; pnex = Pnext;
  //   re = reset

  // Notes on the sheet:
  //   contents of lookuptable_1 (hex, n*v repeats v):
  //   0,1,2,0,3
  //   contents of lookuptable_2 (hex, n*v repeats v):
  //   0,5,a,0,14
endmodule
