// Digital circuit VendingMachine.dig as structural Verilog
module VendingMachine (
  input  P5,
  input  reset,
  input  clock,
  input  P10,
  input  P20,
  input  Pcoffee,
  input  Ptea,
  input  Pchange,
  input  Pnext,
  output [5:0] Balance,
  output CoffeeOut,
  output TeaOut,
  output [1:0] Change5,
  output [1:0] Change10,
  output [1:0] Change20
);

  wire _0001_A, _0001_B, _0001_C, _0001_D, _0111_A, _0111_B, _0111_C, _0111_D, _1101_A, _1101_B, _1101_C,
       _1101_D, A, and_1_out, and_2_out, and_3_out, and_4_out, and_5_out, and_6_out, and_7_out, B, C,
       comparator_1_eq, comparator_1_gt, comparator_2_eq, comparator_2_gt, comparator_3_eq, comparator_3_gt,
       comparator_4_eq, comparator_4_gt, comparator_5_eq, comparator_5_gt, comparator_6_eq, comparator_6_lt,
       comparator_7_eq, comparator_7_lt, comparator_8_eq, comparator_8_lt, D, d_ff_7_nq, d_ff_8_nq,
       d_ff_9_nq, d_ff_10_nq, d_ff_11_nq, d_ff_12_nq, d_ff_13_nq, multiplexer_8_out, multiplexer_15_out,
       multiplexer_25_out, multiplexer_26_out, multiplexer_27_out, multiplexer_28_out, or_1_out, or_2_out,
       or_3_out, or_4_out, or_5_out, or_6_out, or_7_out, or_8_out, P5_t, P10_t, P20_t, Pchange_t, Pcoffee_t,
       Pnext_t, Ptea_t;
  wire [1:0] add_1_s, add_5_s, add_6_s, multiplexer_4_out, multiplexer_11_out, multiplexer_18_out;
  wire [3:0] multiplexer_1_out, multiplexer_2_out, multiplexer_5_out, multiplexer_6_out, multiplexer_9_out,
       multiplexer_10_out, multiplexer_12_out, multiplexer_13_out, multiplexer_16_out, multiplexer_17_out,
       multiplexer_19_out, multiplexer_20_out, multiplexer_21_out, multiplexer_22_out, multiplexer_23_out;
  wire [5:0] _5, _10, _20, _25, multiplexer_14_out, plus_5, plus_10, plus_20;

  Comparator #(.Bits(6)) comparator_1 (
    .a(Balance), .b(6'b000101), .gt(comparator_1_gt), .eq(comparator_1_eq));  // open: lt
  or or_1 (or_1_out, comparator_1_gt, comparator_1_eq);
  Comparator #(.Bits(6)) comparator_2 (
    .a(Balance), .b(6'b001010), .gt(comparator_2_gt), .eq(comparator_2_eq));  // open: lt
  or or_2 (or_2_out, comparator_2_gt, comparator_2_eq);
  Comparator #(.Bits(6)) comparator_3 (
    .a(Balance), .b(6'b010100), .gt(comparator_3_gt), .eq(comparator_3_eq));  // open: lt
  Multiplexer #(.Bits(4)) multiplexer_1 (.sel(or_1_out), .in_0(4'b0001), .in_1(4'b1001), .out(multiplexer_1_out));
  or or_3 (or_3_out, comparator_3_gt, comparator_3_eq);
  Multiplexer #(.Bits(4)) multiplexer_2 (
    .sel(or_2_out), .in_0(multiplexer_1_out), .in_1(4'b1000), .out(multiplexer_2_out));
  Multiplexer #(.Bits(4)) multiplexer_3 (
    .sel(or_3_out), .in_0(multiplexer_2_out), .in_1(4'b1100), .out({_1101_D, _1101_C, _1101_B, _1101_A}));
  Add #(.Bits(2)) add_1 (.a(Change5), .b(2'b01), .c_i(1'b0), .s(add_1_s));  // open: c_o
  Multiplexer #(.Selector_Bits(4), .Bits(2)) multiplexer_4 (
    .sel({D, C, B, A}), .in_0(2'b00), .in_1(Change5), .in_2(Change5), .in_3(Change5), .in_4(Change5),
    .in_5(Change5), .in_6(Change5), .in_7(Change5), .in_8(Change5), .in_9(add_1_s), .in_10(Change5),
    .in_11(Change5), .in_12(Change5), .in_13(Change5), .in_14(Change5), .in_15(2'b00), .out(multiplexer_4_out));
  Multiplexer #(.Bits(4)) multiplexer_5 (.sel(Pchange_t), .in_0({D, C, B, A}), .in_1(4'b1111), .out(multiplexer_5_out));
  D_FF #(.Bits(2)) d_ff_1 (.D(multiplexer_4_out), .C(clock), .Q(Change5));  // open: nQ
  Multiplexer #(.Bits(4)) multiplexer_6 (
    .sel(Pnext_t), .in_0(multiplexer_5_out), .in_1(4'b0001), .out(multiplexer_6_out));
  Add #(.Bits(6)) add_2 (.a(Balance), .b(6'b010100), .c_i(1'b0), .s(plus_20));  // open: c_o
  Add #(.Bits(6)) add_3 (.a(Balance), .b(6'b001010), .c_i(1'b0), .s(plus_10));  // open: c_o
  Add #(.Bits(6)) add_4 (.a(Balance), .b(6'b000101), .c_i(1'b0), .s(plus_5));  // open: c_o
  Comparator #(.Bits(6)) comparator_4 (
    .a(Balance), .b(6'b010100), .gt(comparator_4_gt), .eq(comparator_4_eq));  // open: lt
  Multiplexer #(.Bits(4)) multiplexer_7 (
    .sel(reset), .in_0(multiplexer_6_out), .in_1(4'b0000), .out({_0111_D, _0111_C, _0111_B, _0111_A}));
  Multiplexer #(.Selector_Bits(4)) multiplexer_8 (
    .sel({D, C, B, A}), .in_0(1'b0), .in_1(1'b0), .in_2(CoffeeOut), .in_3(CoffeeOut), .in_4(CoffeeOut),
    .in_5(1'b1), .in_6(CoffeeOut), .in_7(CoffeeOut), .in_8(CoffeeOut), .in_9(CoffeeOut), .in_10(CoffeeOut),
    .in_11(CoffeeOut), .in_12(CoffeeOut), .in_13(CoffeeOut), .in_14(CoffeeOut), .in_15(CoffeeOut),
    .out(multiplexer_8_out));
  or or_4 (or_4_out, comparator_4_gt, comparator_4_eq);
  Add #(.Bits(2)) add_5 (.a(Change10), .b(2'b01), .c_i(1'b0), .s(add_5_s));  // open: c_o
  D_FF d_ff_2 (.D(multiplexer_8_out), .C(clock), .Q(CoffeeOut));  // open: nQ
  Multiplexer #(.Bits(4)) multiplexer_9 (.sel(Pchange_t), .in_0({D, C, B, A}), .in_1(4'b1111), .out(multiplexer_9_out));
  Comparator #(.Bits(6)) comparator_5 (
    .a(Balance), .b(6'b011001), .gt(comparator_5_gt), .eq(comparator_5_eq));  // open: lt
  Sub #(.Bits(6)) sub_1 (.a(Balance), .b(6'b011001), .c_i(1'b0), .s(_25));  // open: c_o
  Sub #(.Bits(6)) sub_2 (.a(Balance), .b(6'b010100), .c_i(1'b0), .s(_20));  // open: c_o
  Sub #(.Bits(6)) sub_3 (.a(Balance), .b(6'b001010), .c_i(1'b0), .s(_10));  // open: c_o
  Sub #(.Bits(6)) sub_4 (.a(Balance), .b(6'b000101), .c_i(1'b0), .s(_5));  // open: c_o
  Multiplexer #(.Bits(4)) multiplexer_10 (
    .sel(or_4_out), .in_0(multiplexer_9_out), .in_1(4'b0110), .out(multiplexer_10_out));
  or or_5 (or_5_out, comparator_5_gt, comparator_5_eq);
  Multiplexer #(.Selector_Bits(4), .Bits(2)) multiplexer_11 (
    .sel({D, C, B, A}), .in_0(2'b00), .in_1(Change10), .in_2(Change10), .in_3(Change10), .in_4(Change10),
    .in_5(Change10), .in_6(Change10), .in_7(Change10), .in_8(add_5_s), .in_9(Change10), .in_10(Change10),
    .in_11(Change10), .in_12(Change10), .in_13(Change10), .in_14(Change10), .in_15(2'b00),
    .out(multiplexer_11_out));
  Multiplexer #(.Bits(4)) multiplexer_12 (
    .sel(Ptea_t), .in_0(multiplexer_9_out), .in_1(multiplexer_10_out), .out(multiplexer_12_out));
  Comparator #(.Bits(6)) comparator_6 (
    .a(Balance), .b(6'b011110), .eq(comparator_6_eq), .lt(comparator_6_lt));  // open: gt
  D_FF #(.Bits(2)) d_ff_3 (.D(multiplexer_11_out), .C(clock), .Q(Change10));  // open: nQ
  Multiplexer #(.Bits(4)) multiplexer_13 (
    .sel(or_5_out), .in_0(multiplexer_12_out), .in_1(4'b0101), .out(multiplexer_13_out));
  or or_6 (or_6_out, comparator_6_eq, comparator_6_lt);
  Multiplexer #(.Selector_Bits(4), .Bits(6)) multiplexer_14 (
    .sel({D, C, B, A}), .in_0({6{1'b0}}), .in_1(Balance), .in_2(plus_5), .in_3(plus_10), .in_4(plus_20),
    .in_5(_25), .in_6(_20), .in_7(Balance), .in_8(_10), .in_9(_5), .in_10(Balance), .in_11(Balance),
    .in_12(_20), .in_13(Balance), .in_14(Balance), .in_15(Balance), .out(multiplexer_14_out));
  Multiplexer #(.Selector_Bits(4)) multiplexer_15 (
    .sel({D, C, B, A}), .in_0(1'b0), .in_1(1'b0), .in_2(TeaOut), .in_3(TeaOut), .in_4(TeaOut), .in_5(TeaOut),
    .in_6(1'b1), .in_7(TeaOut), .in_8(TeaOut), .in_9(TeaOut), .in_10(TeaOut), .in_11(TeaOut), .in_12(TeaOut),
    .in_13(TeaOut), .in_14(TeaOut), .in_15(TeaOut), .out(multiplexer_15_out));
  Multiplexer #(.Bits(4)) multiplexer_16 (
    .sel(Pcoffee_t), .in_0(multiplexer_12_out), .in_1(multiplexer_13_out), .out(multiplexer_16_out));
  Comparator #(.Bits(6)) comparator_7 (
    .a(Balance), .b(6'b101000), .eq(comparator_7_eq), .lt(comparator_7_lt));  // open: gt
  D_FF d_ff_4 (.D(multiplexer_15_out), .C(clock), .Q(TeaOut));  // open: nQ
  or or_7 (or_7_out, comparator_7_eq, comparator_7_lt);
  D_FF #(.Bits(6)) d_ff_5 (.D(multiplexer_14_out), .C(clock), .Q(Balance));  // open: nQ
  Add #(.Bits(2)) add_6 (.a(Change20), .b(2'b01), .c_i(1'b0), .s(add_6_s));  // open: c_o
  Multiplexer #(.Bits(4)) multiplexer_17 (
    .sel(or_6_out), .in_0(multiplexer_16_out), .in_1(4'b0100), .out(multiplexer_17_out));
  Comparator #(.Bits(6)) comparator_8 (
    .a(Balance), .b(6'b101101), .eq(comparator_8_eq), .lt(comparator_8_lt));  // open: gt
  Multiplexer #(.Selector_Bits(4), .Bits(2)) multiplexer_18 (
    .sel({D, C, B, A}), .in_0(2'b00), .in_1(Change20), .in_2(Change20), .in_3(Change20), .in_4(Change20),
    .in_5(Change20), .in_6(Change20), .in_7(Change20), .in_8(Change20), .in_9(Change20), .in_10(Change20),
    .in_11(Change20), .in_12(add_6_s), .in_13(Change20), .in_14(Change20), .in_15(2'b00),
    .out(multiplexer_18_out));
  Multiplexer #(.Bits(4)) multiplexer_19 (
    .sel(P20_t), .in_0(multiplexer_16_out), .in_1(multiplexer_17_out), .out(multiplexer_19_out));
  Multiplexer #(.Bits(4)) multiplexer_20 (
    .sel(or_7_out), .in_0(multiplexer_19_out), .in_1(4'b0011), .out(multiplexer_20_out));
  or or_8 (or_8_out, comparator_8_eq, comparator_8_lt);
  D_FF #(.Bits(2)) d_ff_6 (.D(multiplexer_18_out), .C(clock), .Q(Change20));  // open: nQ
  Multiplexer #(.Bits(4)) multiplexer_21 (
    .sel(P10_t), .in_0(multiplexer_19_out), .in_1(multiplexer_20_out), .out(multiplexer_21_out));
  Multiplexer #(.Bits(4)) multiplexer_22 (
    .sel(or_8_out), .in_0(multiplexer_21_out), .in_1(4'b0010), .out(multiplexer_22_out));
  and and_1 (and_1_out, ~reset, P5);  // And
  and and_2 (and_2_out, ~reset, P10);  // And
  and and_3 (and_3_out, ~reset, P20);  // And
  and and_4 (and_4_out, ~reset, Pcoffee);  // And
  and and_5 (and_5_out, ~reset, Ptea);  // And
  and and_6 (and_6_out, ~reset, Pchange);  // And
  and and_7 (and_7_out, ~reset, Pnext);  // And
  Multiplexer #(.Bits(4)) multiplexer_23 (
    .sel(P5_t), .in_0(multiplexer_21_out), .in_1(multiplexer_22_out), .out(multiplexer_23_out));
  Multiplexer #(.Bits(4)) multiplexer_24 (
    .sel(reset), .in_0(multiplexer_23_out), .in_1(4'b0000), .out({_0001_D, _0001_C, _0001_B, _0001_A}));
  D_FF d_ff_7 (.D(and_1_out), .C(clock), .nQ(d_ff_7_nq));  // open: Q
  D_FF d_ff_8 (.D(and_2_out), .C(clock), .nQ(d_ff_8_nq));  // open: Q
  D_FF d_ff_9 (.D(and_3_out), .C(clock), .nQ(d_ff_9_nq));  // open: Q
  D_FF d_ff_10 (.D(and_4_out), .C(clock), .nQ(d_ff_10_nq));  // open: Q
  D_FF d_ff_11 (.D(and_5_out), .C(clock), .nQ(d_ff_11_nq));  // open: Q
  D_FF d_ff_12 (.D(and_6_out), .C(clock), .nQ(d_ff_12_nq));  // open: Q
  D_FF d_ff_13 (.D(and_7_out), .C(clock), .nQ(d_ff_13_nq));  // open: Q
  and and_8 (P5_t, and_1_out, d_ff_7_nq);
  and and_9 (P10_t, and_2_out, d_ff_8_nq);
  and and_10 (P20_t, and_3_out, d_ff_9_nq);
  and and_11 (Pcoffee_t, and_4_out, d_ff_10_nq);
  and and_12 (Ptea_t, and_5_out, d_ff_11_nq);
  and and_13 (Pchange_t, and_6_out, d_ff_12_nq);
  and and_14 (Pnext_t, and_7_out, d_ff_13_nq);
  Multiplexer #(.Selector_Bits(4)) multiplexer_25 (
    .sel({D, C, B, A}), .in_0(1'b0), .in_1(_0001_D), .in_2(1'b0), .in_3(1'b0), .in_4(1'b0), .in_5(1'b0),
    .in_6(1'b0), .in_7(_0111_D), .in_8(1'b1), .in_9(1'b1), .in_10(1'b0), .in_11(1'b0), .in_12(1'b1),
    .in_13(_1101_D), .in_14(1'b0), .in_15(1'b1), .out(multiplexer_25_out));
  Multiplexer #(.Selector_Bits(4)) multiplexer_26 (
    .sel({D, C, B, A}), .in_0(1'b0), .in_1(_0001_C), .in_2(1'b0), .in_3(1'b0), .in_4(1'b0), .in_5(1'b1),
    .in_6(1'b1), .in_7(_0111_C), .in_8(1'b0), .in_9(1'b1), .in_10(1'b0), .in_11(1'b0), .in_12(1'b1),
    .in_13(_1101_C), .in_14(1'b0), .in_15(1'b1), .out(multiplexer_26_out));
  Multiplexer #(.Selector_Bits(4)) multiplexer_27 (
    .sel({D, C, B, A}), .in_0(1'b0), .in_1(_0001_B), .in_2(1'b0), .in_3(1'b0), .in_4(1'b0), .in_5(1'b1),
    .in_6(1'b1), .in_7(_0111_B), .in_8(1'b0), .in_9(1'b0), .in_10(1'b0), .in_11(1'b0), .in_12(1'b0),
    .in_13(_1101_B), .in_14(1'b0), .in_15(1'b0), .out(multiplexer_27_out));
  Multiplexer #(.Selector_Bits(4)) multiplexer_28 (
    .sel({D, C, B, A}), .in_0(1'b1), .in_1(_0001_A), .in_2(1'b1), .in_3(1'b1), .in_4(1'b1), .in_5(1'b1),
    .in_6(1'b1), .in_7(_0111_A), .in_8(1'b0), .in_9(1'b1), .in_10(1'b0), .in_11(1'b0), .in_12(1'b1),
    .in_13(_1101_A), .in_14(1'b0), .in_15(1'b1), .out(multiplexer_28_out));
  // Probe State on {D, C, B, A}
  // Probe State on {D, C, B, A}
  D_FF d_ff_14 (.D(multiplexer_25_out), .C(clock), .Q(D));  // open: nQ
  D_FF d_ff_15 (.D(multiplexer_26_out), .C(clock), .Q(C));  // open: nQ
  D_FF d_ff_16 (.D(multiplexer_27_out), .C(clock), .Q(B));  // open: nQ
  D_FF d_ff_17 (.D(multiplexer_28_out), .C(clock), .Q(A));  // open: nQ

  // Other names for the same wires on the sheet: State[3:0] = {D, C, B, A}; clk = clock
endmodule
