// Digital circuit mark1.dig as structural Verilog
module mark1 (
  input  P5,
  input  reset,
  input  clock,
  input  P10,
  input  P20,
  input  Pcoffee,
  input  Ptea,
  input  Pchange,
  input  Pnext,
  output [5:0] Balance,
  output CoffeeOut,
  output TeaOut,
  output [1:0] Change5,
  output [1:0] Change10,
  output [1:0] Change20
);

  wire _0001_A, _0001_B, _0001_C, _0001_D, _0111_A, _0111_B, _0111_C, _0111_D, _1101_A, _1101_B, _1101_C,
       _1101_D, A, B, C, comparator_1_eq, comparator_1_gt, comparator_2_eq, comparator_2_gt, comparator_3_eq,
       comparator_3_lt, comparator_4_eq, comparator_4_lt, comparator_5_eq, comparator_5_lt, comparator_6_eq,
       comparator_6_gt, comparator_7_eq, comparator_7_gt, comparator_8_eq, comparator_8_gt, D, or_1_out,
       or_2_out, or_3_out, or_4_out, or_5_out, or_6_out, or_7_out, or_8_out;
  wire [1:0] add_2_s, multiplexer_1_out;
  wire [3:0] _0001, _0111, _1101, multiplexer_4_out, multiplexer_5_out, multiplexer_6_out, multiplexer_7_out,
       multiplexer_8_out, multiplexer_9_out, multiplexer_10_out, multiplexer_11_out, multiplexer_12_out,
       multiplexer_13_out, multiplexer_15_out, multiplexer_16_out, multiplexer_17_out, multiplexer_18_out,
       multiplexer_20_out, multiplexer_22_out;
  wire [3:2] add_1_s;
  wire [5:0] _5, _10, _20, _25, multiplexer_2_out, multiplexer_3_out, plus_5, plus_10, plus_20;
  wire [5:4] add_3_s;

  Multiplexer #(.Selector_Bits(4), .Bits(2)) multiplexer_1 (
    .sel({D, C, B, A}), .in_0(2'b00), .in_1(2'b00), .in_2({CoffeeOut, TeaOut}), .in_3({CoffeeOut, TeaOut}),
    .in_4({CoffeeOut, TeaOut}), .in_5({1'b1, TeaOut}), .in_6({CoffeeOut, 1'b1}), .in_7({CoffeeOut, TeaOut}),
    .in_8({CoffeeOut, TeaOut}), .in_9({CoffeeOut, TeaOut}), .in_10({CoffeeOut, TeaOut}),
    .in_11({CoffeeOut, TeaOut}), .in_12({CoffeeOut, TeaOut}), .in_13({CoffeeOut, TeaOut}),
    .in_14({CoffeeOut, TeaOut}), .in_15({CoffeeOut, TeaOut}), .out(multiplexer_1_out));
  D_FF #(.Bits(2)) d_ff_1 (.D(multiplexer_1_out), .C(clock), .Q({CoffeeOut, TeaOut}));  // open: nQ
  Add #(.Bits(2)) add_1 (.a(Change10), .b(2'b01), .c_i(1'b0), .s(add_1_s));  // open: c_o
  Add #(.Bits(2)) add_2 (.a(Change5), .b(2'b01), .c_i(1'b0), .s(add_2_s));  // open: c_o
  Add #(.Bits(2)) add_3 (.a(Change20), .b(2'b01), .c_i(1'b0), .s(add_3_s));  // open: c_o
  Multiplexer #(.Selector_Bits(4), .Bits(6)) multiplexer_2 (
    .sel({D, C, B, A}), .in_0({6{1'b0}}), .in_1({Change20, Change10, Change5}),
    .in_2({Change20, Change10, Change5}), .in_3({Change20, Change10, Change5}),
    .in_4({Change20, Change10, Change5}), .in_5({Change20, Change10, Change5}),
    .in_6({Change20, Change10, Change5}), .in_7({Change20, Change10, Change5}),
    .in_8({Change20, add_1_s, Change5}), .in_9({Change20, Change10, add_2_s}),
    .in_10({Change20, Change10, Change5}), .in_11({Change20, Change10, Change5}),
    .in_12({add_3_s, Change10, Change5}), .in_13({Change20, Change10, Change5}),
    .in_14({Change20, Change10, Change5}), .in_15({6{1'b0}}), .out(multiplexer_2_out));
  D_FF #(.Bits(6)) d_ff_2 (.D(multiplexer_2_out), .C(clock), .Q({Change20, Change10, Change5}));  // open: nQ
  Multiplexer #(.Selector_Bits(4), .Bits(6)) multiplexer_3 (
    .sel({D, C, B, A}), .in_0({6{1'b0}}), .in_1(Balance), .in_2(plus_5), .in_3(plus_10), .in_4(plus_20),
    .in_5(_25), .in_6(_20), .in_7(Balance), .in_8(_10), .in_9(_5), .in_10(Balance), .in_11(Balance),
    .in_12(_20), .in_13(Balance), .in_14(Balance), .in_15(Balance), .out(multiplexer_3_out));
  Comparator #(.Bits(6)) comparator_1 (
    .a(Balance), .b(6'b010100), .gt(comparator_1_gt), .eq(comparator_1_eq));  // open: lt
  or or_1 (or_1_out, comparator_1_gt, comparator_1_eq);
  Comparator #(.Bits(6)) comparator_2 (
    .a(Balance), .b(6'b011001), .gt(comparator_2_gt), .eq(comparator_2_eq));  // open: lt
  D_FF #(.Bits(6)) d_ff_3 (.D(multiplexer_3_out), .C(clock), .Q(Balance));  // open: nQ
  Multiplexer #(.Bits(4)) multiplexer_4 (.sel(Pchange), .in_0({D, C, B, A}), .in_1(4'b1111), .out(multiplexer_4_out));
  Multiplexer #(.Bits(4)) multiplexer_5 (
    .sel(or_1_out), .in_0(multiplexer_4_out), .in_1(4'b0110), .out(multiplexer_5_out));
  or or_2 (or_2_out, comparator_2_gt, comparator_2_eq);
  Comparator #(.Bits(6)) comparator_3 (
    .a(Balance), .b(6'b011110), .eq(comparator_3_eq), .lt(comparator_3_lt));  // open: gt
  Sub #(.Bits(6)) sub_1 (.a(Balance), .b(6'b011001), .c_i(1'b0), .s(_25));  // open: c_o
  Sub #(.Bits(6)) sub_2 (.a(Balance), .b(6'b010100), .c_i(1'b0), .s(_20));  // open: c_o
  Sub #(.Bits(6)) sub_3 (.a(Balance), .b(6'b001010), .c_i(1'b0), .s(_10));  // open: c_o
  Sub #(.Bits(6)) sub_4 (.a(Balance), .b(6'b000101), .c_i(1'b0), .s(_5));  // open: c_o
  Add #(.Bits(6)) add_4 (.a(Balance), .b(6'b010100), .c_i(1'b0), .s(plus_20));  // open: c_o
  Add #(.Bits(6)) add_5 (.a(Balance), .b(6'b001010), .c_i(1'b0), .s(plus_10));  // open: c_o
  Add #(.Bits(6)) add_6 (.a(Balance), .b(6'b000101), .c_i(1'b0), .s(plus_5));  // open: c_o
  Multiplexer #(.Bits(4)) multiplexer_6 (
    .sel(Ptea), .in_0(multiplexer_4_out), .in_1(multiplexer_5_out), .out(multiplexer_6_out));
  Multiplexer #(.Bits(4)) multiplexer_7 (
    .sel(or_2_out), .in_0(multiplexer_6_out), .in_1(4'b0101), .out(multiplexer_7_out));
  or or_3 (or_3_out, comparator_3_eq, comparator_3_lt);
  Comparator #(.Bits(6)) comparator_4 (
    .a(Balance), .b(6'b101000), .eq(comparator_4_eq), .lt(comparator_4_lt));  // open: gt
  Multiplexer #(.Bits(4)) multiplexer_8 (
    .sel(Pcoffee), .in_0(multiplexer_6_out), .in_1(multiplexer_7_out), .out(multiplexer_8_out));
  Multiplexer #(.Bits(4)) multiplexer_9 (
    .sel(or_3_out), .in_0(multiplexer_8_out), .in_1(4'b0100), .out(multiplexer_9_out));
  or or_4 (or_4_out, comparator_4_eq, comparator_4_lt);
  Multiplexer #(.Bits(4)) multiplexer_10 (.sel(Pchange), .in_0({D, C, B, A}), .in_1(4'b1111), .out(multiplexer_10_out));
  Multiplexer #(.Bits(4)) multiplexer_11 (
    .sel(Pnext), .in_0(multiplexer_10_out), .in_1(4'b0001), .out(multiplexer_11_out));
  Multiplexer #(.Bits(4)) multiplexer_12 (
    .sel(P20), .in_0(multiplexer_8_out), .in_1(multiplexer_9_out), .out(multiplexer_12_out));
  Multiplexer #(.Bits(4)) multiplexer_13 (
    .sel(or_4_out), .in_0(multiplexer_12_out), .in_1(4'b0011), .out(multiplexer_13_out));
  Comparator #(.Bits(6)) comparator_5 (
    .a(Balance), .b(6'b101101), .eq(comparator_5_eq), .lt(comparator_5_lt));  // open: gt
  Multiplexer #(.Bits(4)) multiplexer_14 (
    .sel(reset), .in_0(multiplexer_11_out), .in_1(4'b0000), .out({_0111_D, _0111_C, _0111_B, _0111_A}));
  Comparator #(.Bits(6)) comparator_6 (
    .a(Balance), .b(6'b000101), .gt(comparator_6_gt), .eq(comparator_6_eq));  // open: lt
  Multiplexer #(.Bits(4)) multiplexer_15 (
    .sel(P10), .in_0(multiplexer_12_out), .in_1(multiplexer_13_out), .out(multiplexer_15_out));
  or or_5 (or_5_out, comparator_5_eq, comparator_5_lt);
  Comparator #(.Bits(6)) comparator_7 (
    .a(Balance), .b(6'b001010), .gt(comparator_7_gt), .eq(comparator_7_eq));  // open: lt
  Comparator #(.Bits(6)) comparator_8 (
    .a(Balance), .b(6'b010100), .gt(comparator_8_gt), .eq(comparator_8_eq));  // open: lt
  Multiplexer #(.Bits(4)) multiplexer_16 (
    .sel(P5), .in_0(multiplexer_15_out), .in_1(multiplexer_17_out), .out(multiplexer_16_out));
  Multiplexer #(.Bits(4)) multiplexer_17 (
    .sel(or_5_out), .in_0(multiplexer_15_out), .in_1(4'b0010), .out(multiplexer_17_out));
  Multiplexer #(.Bits(4)) multiplexer_18 (.sel(or_6_out), .in_0(4'b0001), .in_1(4'b1001), .out(multiplexer_18_out));
  or or_6 (or_6_out, comparator_6_gt, comparator_6_eq);
  or or_7 (or_7_out, comparator_7_gt, comparator_7_eq);
  Multiplexer #(.Bits(4)) multiplexer_19 (
    .sel(reset), .in_0(multiplexer_16_out), .in_1(4'b0000), .out({_0001_D, _0001_C, _0001_B, _0001_A}));
  Multiplexer #(.Bits(4)) multiplexer_20 (
    .sel(or_7_out), .in_0(multiplexer_18_out), .in_1(4'b1000), .out(multiplexer_20_out));
  Multiplexer #(.Bits(4)) multiplexer_21 (
    .sel(or_8_out), .in_0(multiplexer_20_out), .in_1(4'b1100), .out({_1101_D, _1101_C, _1101_B, _1101_A}));
  or or_8 (or_8_out, comparator_8_gt, comparator_8_eq);
  Multiplexer #(.Selector_Bits(4), .Bits(4)) multiplexer_22 (
    .sel({D, C, B, A}), .in_0(4'b0000), .in_1(_0001), .in_2(4'b0001), .in_3(4'b0001), .in_4(4'b0001),
    .in_5(4'b0111), .in_6(4'b0111), .in_7(_0111), .in_8(4'b1101), .in_9(4'b1101), .in_10(4'b0000),
    .in_11(4'b0000), .in_12(4'b1101), .in_13(_1101), .in_14(4'b0000), .in_15(4'b1101),
    .out(multiplexer_22_out));
  D_FF #(.Bits(4)) d_ff_4 (.D(multiplexer_22_out), .C(clock), .Q({D, C, B, A}));  // open: nQ

  // Other names for the same wires on the sheet: State[3:0] = {D, C, B, A};
  //   C6bit[5:0] = {Change20, Change10, Change5}; clk = clock; CTO2bit[1:0] = {CoffeeOut, TeaOut}
endmodule
