// Digital circuit testMemory.dig as structural Verilog
module testMemory (
  input  P5,
  input  reset,
  input  clock,
  input  P10,
  input  P20,
  input  Pcoffee,
  input  Ptea,
  input  Pchange,
  input  Pnext,
  output [5:0] Balance,
  output CoffeeOut,
  output TeaOut,
  output [1:0] Change5,
  output [1:0] Change10,
  output [1:0] Change20
);

  wire and_1_out, and_2_out, and_3_out, and_4_out, and_5_out, and_6_out, and_7_out, comparator_1_eq,
       comparator_1_gt, comparator_2_eq, comparator_2_gt, comparator_3_eq, comparator_3_gt, comparator_4_eq,
       comparator_4_gt, comparator_5_eq, comparator_5_gt, comparator_6_eq, comparator_6_lt, comparator_7_eq,
       comparator_7_lt, comparator_8_eq, comparator_8_lt, d_ff_4_nq, d_ff_5_nq, d_ff_6_nq, d_ff_7_nq,
       d_ff_8_nq, d_ff_9_nq, d_ff_10_nq, or_1_out, or_2_out, or_3_out, or_4_out, or_5_out, or_6_out,
       or_7_out, or_8_out, P5_t, P10_t, P20_t, Pchange_t, Pcoffee_t, Pnext_t, Ptea_t;
  wire [1:0] add_5_s, multiplexer_4_out;
  wire [3:0] _0001, _0111, _1101, multiplexer_1_out, multiplexer_2_out, multiplexer_5_out, multiplexer_6_out,
       multiplexer_8_out, multiplexer_9_out, multiplexer_10_out, multiplexer_11_out, multiplexer_13_out,
       multiplexer_14_out, multiplexer_15_out, multiplexer_17_out, multiplexer_18_out, multiplexer_19_out,
       multiplexer_20_out, multiplexer_22_out, State;
  wire [3:2] add_4_s;
  wire [5:0] _5, _10, _20, _25, multiplexer_12_out, multiplexer_16_out, plus_5, plus_10, plus_20;
  wire [5:4] add_6_s;

  Comparator #(.Bits(6)) comparator_1 (
    .a(Balance), .b(6'b000101), .gt(comparator_1_gt), .eq(comparator_1_eq));  // open: lt
  or or_1 (or_1_out, comparator_1_gt, comparator_1_eq);
  Multiplexer #(.Bits(4)) multiplexer_1 (.sel(or_1_out), .in_0(4'b0001), .in_1(4'b1001), .out(multiplexer_1_out));
  Comparator #(.Bits(6)) comparator_2 (
    .a(Balance), .b(6'b001010), .gt(comparator_2_gt), .eq(comparator_2_eq));  // open: lt
  or or_2 (or_2_out, comparator_2_gt, comparator_2_eq);
  Multiplexer #(.Bits(4)) multiplexer_2 (
    .sel(or_2_out), .in_0(multiplexer_1_out), .in_1(4'b1000), .out(multiplexer_2_out));
  Comparator #(.Bits(6)) comparator_3 (
    .a(Balance), .b(6'b010100), .gt(comparator_3_gt), .eq(comparator_3_eq));  // open: lt
  or or_3 (or_3_out, comparator_3_gt, comparator_3_eq);
  Multiplexer #(.Bits(4)) multiplexer_3 (.sel(or_3_out), .in_0(multiplexer_2_out), .in_1(4'b1100), .out(_1101));
  Multiplexer #(.Selector_Bits(4), .Bits(2)) multiplexer_4 (
    .sel(State), .in_0(2'b00), .in_1(2'b00), .in_2({CoffeeOut, TeaOut}), .in_3({CoffeeOut, TeaOut}),
    .in_4({CoffeeOut, TeaOut}), .in_5({1'b1, TeaOut}), .in_6({CoffeeOut, 1'b1}), .in_7({CoffeeOut, TeaOut}),
    .in_8({CoffeeOut, TeaOut}), .in_9({CoffeeOut, TeaOut}), .in_10({CoffeeOut, TeaOut}),
    .in_11({CoffeeOut, TeaOut}), .in_12({CoffeeOut, TeaOut}), .in_13({CoffeeOut, TeaOut}),
    .in_14({CoffeeOut, TeaOut}), .in_15({CoffeeOut, TeaOut}), .out(multiplexer_4_out));
  Multiplexer #(.Bits(4)) multiplexer_5 (.sel(Pchange_t), .in_0(State), .in_1(4'b1111), .out(multiplexer_5_out));
  Multiplexer #(.Bits(4)) multiplexer_6 (
    .sel(Pnext_t), .in_0(multiplexer_5_out), .in_1(4'b0001), .out(multiplexer_6_out));
  D_FF #(.Bits(2)) d_ff_1 (.D(multiplexer_4_out), .C(clock), .Q({CoffeeOut, TeaOut}));  // open: nQ
  Multiplexer #(.Bits(4)) multiplexer_7 (.sel(reset), .in_0(multiplexer_6_out), .in_1(4'b0000), .out(_0111));
  Add #(.Bits(6)) add_1 (.a(Balance), .b(6'b010100), .c_i(1'b0), .s(plus_20));  // open: c_o
  Add #(.Bits(6)) add_2 (.a(Balance), .b(6'b001010), .c_i(1'b0), .s(plus_10));  // open: c_o
  Add #(.Bits(6)) add_3 (.a(Balance), .b(6'b000101), .c_i(1'b0), .s(plus_5));  // open: c_o
  Multiplexer #(.Bits(4)) multiplexer_8 (.sel(Pchange_t), .in_0(State), .in_1(4'b1111), .out(multiplexer_8_out));
  Comparator #(.Bits(6)) comparator_4 (
    .a(Balance), .b(6'b010100), .gt(comparator_4_gt), .eq(comparator_4_eq));  // open: lt
  Sub #(.Bits(6)) sub_1 (.a(Balance), .b(6'b011001), .c_i(1'b0), .s(_25));  // open: c_o
  Sub #(.Bits(6)) sub_2 (.a(Balance), .b(6'b010100), .c_i(1'b0), .s(_20));  // open: c_o
  Sub #(.Bits(6)) sub_3 (.a(Balance), .b(6'b001010), .c_i(1'b0), .s(_10));  // open: c_o
  Sub #(.Bits(6)) sub_4 (.a(Balance), .b(6'b000101), .c_i(1'b0), .s(_5));  // open: c_o
  Add #(.Bits(2)) add_4 (.a(Change10), .b(2'b01), .c_i(1'b0), .s(add_4_s));  // open: c_o
  or or_4 (or_4_out, comparator_4_gt, comparator_4_eq);
  Multiplexer #(.Bits(4)) multiplexer_9 (
    .sel(or_4_out), .in_0(multiplexer_8_out), .in_1(4'b0110), .out(multiplexer_9_out));
  Comparator #(.Bits(6)) comparator_5 (
    .a(Balance), .b(6'b011001), .gt(comparator_5_gt), .eq(comparator_5_eq));  // open: lt
  Multiplexer #(.Bits(4)) multiplexer_10 (
    .sel(Ptea_t), .in_0(multiplexer_8_out), .in_1(multiplexer_9_out), .out(multiplexer_10_out));
  or or_5 (or_5_out, comparator_5_gt, comparator_5_eq);
  Add #(.Bits(2)) add_5 (.a(Change5), .b(2'b01), .c_i(1'b0), .s(add_5_s));  // open: c_o
  Multiplexer #(.Bits(4)) multiplexer_11 (
    .sel(or_5_out), .in_0(multiplexer_10_out), .in_1(4'b0101), .out(multiplexer_11_out));
  Comparator #(.Bits(6)) comparator_6 (
    .a(Balance), .b(6'b011110), .eq(comparator_6_eq), .lt(comparator_6_lt));  // open: gt
  Multiplexer #(.Selector_Bits(4), .Bits(6)) multiplexer_12 (
    .sel(State), .in_0({6{1'b0}}), .in_1(Balance), .in_2(plus_5), .in_3(plus_10), .in_4(plus_20), .in_5(_25),
    .in_6(_20), .in_7(Balance), .in_8(_10), .in_9(_5), .in_10(Balance), .in_11(Balance), .in_12(_20),
    .in_13(Balance), .in_14(Balance), .in_15(Balance), .out(multiplexer_12_out));
  Multiplexer #(.Bits(4)) multiplexer_13 (
    .sel(Pcoffee_t), .in_0(multiplexer_10_out), .in_1(multiplexer_11_out), .out(multiplexer_13_out));
  or or_6 (or_6_out, comparator_6_eq, comparator_6_lt);
  D_FF #(.Bits(6)) d_ff_2 (.D(multiplexer_12_out), .C(clock), .Q(Balance));  // open: nQ
  Add #(.Bits(2)) add_6 (.a(Change20), .b(2'b01), .c_i(1'b0), .s(add_6_s));  // open: c_o
  Multiplexer #(.Bits(4)) multiplexer_14 (
    .sel(or_6_out), .in_0(multiplexer_13_out), .in_1(4'b0100), .out(multiplexer_14_out));
  Comparator #(.Bits(6)) comparator_7 (
    .a(Balance), .b(6'b101000), .eq(comparator_7_eq), .lt(comparator_7_lt));  // open: gt
  Multiplexer #(.Bits(4)) multiplexer_15 (
    .sel(P20_t), .in_0(multiplexer_13_out), .in_1(multiplexer_14_out), .out(multiplexer_15_out));
  Multiplexer #(.Selector_Bits(4), .Bits(6)) multiplexer_16 (
    .sel(State), .in_0({6{1'b0}}), .in_1({Change20, Change10, Change5}),
    .in_2({Change20, Change10, Change5}), .in_3({Change20, Change10, Change5}),
    .in_4({Change20, Change10, Change5}), .in_5({Change20, Change10, Change5}),
    .in_6({Change20, Change10, Change5}), .in_7({Change20, Change10, Change5}),
    .in_8({Change20, add_4_s, Change5}), .in_9({Change20, Change10, add_5_s}),
    .in_10({Change20, Change10, Change5}), .in_11({Change20, Change10, Change5}),
    .in_12({add_6_s, Change10, Change5}), .in_13({Change20, Change10, Change5}),
    .in_14({Change20, Change10, Change5}), .in_15({6{1'b0}}), .out(multiplexer_16_out));
  Multiplexer #(.Bits(4)) multiplexer_17 (
    .sel(or_7_out), .in_0(multiplexer_15_out), .in_1(4'b0011), .out(multiplexer_17_out));
  or or_7 (or_7_out, comparator_7_eq, comparator_7_lt);
  D_FF #(.Bits(6)) d_ff_3 (.D(multiplexer_16_out), .C(clock), .Q({Change20, Change10, Change5}));  // open: nQ
  Multiplexer #(.Bits(4)) multiplexer_18 (
    .sel(P10_t), .in_0(multiplexer_15_out), .in_1(multiplexer_17_out), .out(multiplexer_18_out));
  Comparator #(.Bits(6)) comparator_8 (
    .a(Balance), .b(6'b101101), .eq(comparator_8_eq), .lt(comparator_8_lt));  // open: gt
  or or_8 (or_8_out, comparator_8_eq, comparator_8_lt);
  and and_1 (and_1_out, ~reset, P5);  // And
  and and_2 (and_2_out, ~reset, P10);  // And
  and and_3 (and_3_out, ~reset, P20);  // And
  and and_4 (and_4_out, ~reset, Pcoffee);  // And
  and and_5 (and_5_out, ~reset, Ptea);  // And
  and and_6 (and_6_out, ~reset, Pchange);  // And
  and and_7 (and_7_out, ~reset, Pnext);  // And
  Multiplexer #(.Bits(4)) multiplexer_19 (
    .sel(or_8_out), .in_0(multiplexer_18_out), .in_1(4'b0010), .out(multiplexer_19_out));
  Multiplexer #(.Bits(4)) multiplexer_20 (
    .sel(P5_t), .in_0(multiplexer_18_out), .in_1(multiplexer_19_out), .out(multiplexer_20_out));
  D_FF d_ff_4 (.D(and_1_out), .C(clock), .nQ(d_ff_4_nq));  // open: Q
  D_FF d_ff_5 (.D(and_2_out), .C(clock), .nQ(d_ff_5_nq));  // open: Q
  D_FF d_ff_6 (.D(and_3_out), .C(clock), .nQ(d_ff_6_nq));  // open: Q
  D_FF d_ff_7 (.D(and_4_out), .C(clock), .nQ(d_ff_7_nq));  // open: Q
  D_FF d_ff_8 (.D(and_5_out), .C(clock), .nQ(d_ff_8_nq));  // open: Q
  D_FF d_ff_9 (.D(and_6_out), .C(clock), .nQ(d_ff_9_nq));  // open: Q
  D_FF d_ff_10 (.D(and_7_out), .C(clock), .nQ(d_ff_10_nq));  // open: Q
  Multiplexer #(.Bits(4)) multiplexer_21 (.sel(reset), .in_0(multiplexer_20_out), .in_1(4'b0000), .out(_0001));
  and and_8 (P5_t, and_1_out, d_ff_4_nq);
  and and_9 (P10_t, and_2_out, d_ff_5_nq);
  and and_10 (P20_t, and_3_out, d_ff_6_nq);
  and and_11 (Pcoffee_t, and_4_out, d_ff_7_nq);
  and and_12 (Ptea_t, and_5_out, d_ff_8_nq);
  and and_13 (Pchange_t, and_6_out, d_ff_9_nq);
  and and_14 (Pnext_t, and_7_out, d_ff_10_nq);
  Multiplexer #(.Selector_Bits(4), .Bits(4)) multiplexer_22 (
    .sel(State), .in_0(4'b0001), .in_1(_0001), .in_2(4'b0001), .in_3(4'b0001), .in_4(4'b0001),
    .in_5(4'b0111), .in_6(4'b0111), .in_7(_0111), .in_8(4'b1101), .in_9(4'b1101), .in_10(4'b0000),
    .in_11(4'b0000), .in_12(4'b1101), .in_13(_1101), .in_14(4'b0000), .in_15(4'b1101),
    .out(multiplexer_22_out));
  D_FF #(.Bits(4)) d_ff_11 (.D(multiplexer_22_out), .C(clock), .Q(State));  // open: nQ

  // Other names for the same wires on the sheet: C6bit[5:0] = {Change20, Change10, Change5}; clk = clock;
  //   CTO2bit[1:0] = {CoffeeOut, TeaOut}
endmodule
